// Logisim project salvo.circ as structural Verilog
module main (
  input  X0,
  output out_2
);

  wire and_2_out, and_3_out, and_4_out, and_5_out, clock_1_out, D0, D1, notQ0, notQ1, Q0, Q1;

  and and_1 (out_2, Q0, Q1);
  Clock clock_1 (.out(clock_1_out));
  and and_2 (and_2_out, notQ0, X0);
  and and_3 (and_3_out, X0, Q1);
  D_Flip_Flop u_Q1 (.D(D1), .clk(clock_1_out), .Q(Q1), .Qn(notQ1));  // open: preset, reset
  or or_1 (D0, and_2_out, and_3_out);
  D_Flip_Flop u_Q0 (.D(D0), .clk(clock_1_out), .Q(Q0), .Qn(notQ0));  // open: preset, reset
  and and_4 (and_4_out, Q0, X0);
  and and_5 (and_5_out, X0, Q1);
  or or_2 (D1, and_4_out, and_5_out);

  // Notes on the sheet:
  //   INPUT
  //   OUTPUT
endmodule

// VHDL entity Seq, as the project stores it:
--------------------------------------------------------------------------------
-- Project :
-- File    :
-- Autor   :
-- Date    :
--
--------------------------------------------------------------------------------
-- Description :
--
--------------------------------------------------------------------------------

LIBRARY ieee;
USE ieee.std_logic_1164.all;

ENTITY Seq IS
  PORT (
  ------------------------------------------------------------------------------
  --Insert input ports below
    clock, seq_in      : IN  std_logic;                    -- input bit example
    
    cicle_out          : OUT std_logic_vector(2 downto 0); -- debug
    det_out            : out std_logic
    );
END Seq;

--------------------------------------------------------------------------------
--Complete your VHDL description below
--------------------------------------------------------------------------------

ARCHITECTURE TypeArchitecture OF Seq IS

BEGIN


END TypeArchitecture;
