// Logisim project P10.circ as structural Verilog
module P0_FFD (
);

  comps comps_1 ();  // open: a

  // Notes on the sheet:
  //   Este bloco de entidade VHDL contém duas entidades VHDL:
  //   A segunda chmada "ffd_vhdl", que será usada em todo este projeto:
  //   A primeira chamada "comps", que será renomeada e que não faz nada:
endmodule

module P1_cnt_mod16_up (
);

  wire C, d_ff_1_qn, d_ff_2_qn, d_ff_3_qn, d_ff_4_qn, d_ff_5_q, F_out, FF0_qn, FF1_qn, FF2_qn, FF3_qn,
       not_1_out, not_2_out, or_1_out, or_2_out, Q0, Q1, Q2, Q3, Q4, R, RSTD, Z_out, ZR_out;
  wire [3:0] undriven;

  Clock clock_1 (.out(C));
  D_Flip_Flop FF0 (.D(FF0_qn), .clk(C), .Q(Q0), .Qn(FF0_qn), .preset(or_1_out));  // open: reset
  D_Flip_Flop d_ff_1 (.D(d_ff_1_qn), .clk(C), .Q(Q0), .Qn(d_ff_1_qn), .reset(or_2_out));  // open: preset
  J_K_Flip_Flop j_k_ff_1 (.J(1'b1), .K(1'b0), .clk(Q4), .Q(R), .reset(not_1_out));  // open: Qn, preset
  not not_1 (not_1_out, C);
  D_Flip_Flop FF1 (.D(FF1_qn), .clk(Q0), .Q(Q1), .Qn(FF1_qn), .reset(or_1_out));  // open: preset
  D_Flip_Flop d_ff_2 (.D(d_ff_2_qn), .clk(d_ff_1_qn), .Q(Q1), .Qn(d_ff_2_qn), .reset(or_2_out));  // open: preset
  D_Flip_Flop FF2 (.D(FF2_qn), .clk(Q1), .Q(Q2), .Qn(FF2_qn), .reset(or_1_out));  // open: preset
  D_Flip_Flop d_ff_3 (.D(d_ff_3_qn), .clk(d_ff_2_qn), .Q(Q2), .Qn(d_ff_3_qn), .reset(or_2_out));  // open: preset
  and and_1 (Q4, Q1, Q3, ~Q0, ~Q2);  // AND_Gate
  D_Flip_Flop FF3 (.D(FF3_qn), .clk(Q2), .Q(Q3), .Qn(FF3_qn), .preset(or_1_out));  // open: reset
  or or_1 (or_1_out, not_2_out, RSTD);
  not not_2 (not_2_out, Z_out);
  Button #(.press("passive")) Z (.out(Z_out));
  D_Flip_Flop d_ff_4 (.D(d_ff_4_qn), .clk(d_ff_3_qn), .Q(Q3), .Qn(d_ff_4_qn), .reset(or_2_out));  // open: preset
  buf or_2 (or_2_out, R);  // OR_Gate
  Hex_Digit_Display hex_digit_display_1 (.value({Q3, Q2, Q1, Q0}));  // open: dp
  Hex_Digit_Display hex_digit_display_2 (.value(undriven));  // open: dp
  cnt_up_down_mod10 cnt_up_down_mod10_1 ();  // open: clk, z, ud, q, co
  and F (F_out, Q0, Q1, Q2, Q3);
  nor ZR (ZR_out, Q0, Q1, Q2, Q3);
  D_Flip_Flop d_ff_5 (.Q(d_ff_5_q), .preset(ZR_out), .reset(RSTD));  // open: D, clk, Qn
  and u_R (RSTD, F_out, d_ff_5_q);
endmodule

// VHDL entity comps, as the project stores it:
--------------------------------------------------------------------------------
-- UTFPR - Universidade Tecnológica Federal do Paraná - Curitiba - PR
-- Projeto  : Prática 5 - Cronômetro
-- Circuito : Implementação de um FF tipo D
-- Arquivo  : dff_vhdl.vhd
-- Autor    : prof. Gortan
-- Data     : Outubro 2021
--------------------------------------------------------------------------------
-- Descrição :
-- Implementa um flip-flop tipo D para ser usado como componente em outros circ.
-- obs.: para evitar que o Logisim-evolution 3.6.1 altere o nome do componente
--       introduzimos um componente "comps" no início do arquivo e o ff tipo d
--       vem em segundo lugar - No Quartus ele deve ser comentado / apagado
--------------------------------------------------------------------------------

--============================= Módulo comps: ==================================
library ieee;
  use ieee.std_logic_1164.all;

-- Comentar a entity comps e sua architecture quando usado no Quartus
-- Esse primeira entity é só um artifício para evitar que o Logisim
-- altere o nome do componente ff tipo d, que vem depois
entity comps is
  port(    a  : in  std_logic );
end comps;

architecture cmp_arch of comps is
-- Não faz nada:
begin
end cmp_arch;
-- Fim do trecho a comentar/apagar no Quartus

--==================== Componente: =============================================
library ieee;
  use ieee.std_logic_1164.all;

entity dff_vhdl is
  port(
    d, clk, prs, clr	: in  std_logic;	-- entradas: dado, clk, preset e clear
    q, qn				: out std_logic		-- saídas:   q e q invertido
 );
end dff_vhdl;

architecture ff_d of dff_vhdl is

	signal qstate: std_logic;

begin
	process(clk, clr, prs)
	begin
		if clr = '1' then qstate <= '0';
		elsif prs = '1' then qstate <= '1';
		elsif clk = '1' and clk' event then qstate <= d;
		end if;
	end process;
	q <= qstate;
	qn <= not qstate;
end ff_d;

// VHDL entity cnt_up_down_mod10, as the project stores it:
LIBRARY ieee;
USE ieee.std_logic_1164.all;

ENTITY cnt_up_down_mod10 IS
  PORT (
    	clk, z, ud  : in  std_logic;					-- entradas clk, rst
    	q       : inout std_logic_vector(3 downto 0);	-- saída q3 até q0
	co : out std_logic
    );
END cnt_up_down_mod10;

--------------------------------------------------------------------------------
--Complete your VHDL description below
--------------------------------------------------------------------------------

ARCHITECTURE TypeArchitecture OF cnt_up_down_mod10 IS

	signal zn: std_logic;
	signal qn: std_logic_vector(3 downto 0);	-- liga qn com d
	
	component dff_vhdl is					-- dff referenciado como dff_vhdl
		port
		(
			d, clk, prs, clr	: in  std_logic;	-- entradas: dado, clk, preset e clear
			q, qn			: out std_logic 	-- saídas:   q e q invertido
		);
	end component;
	-- decodificardor
	signal F: std_logic;
	signal ZR: std_logic;
	signal SR: std_logic;
	signal R: std_logic;
	signal S: std_logic;
	--
	-- pulsos reset
	signal RSTE_down: std_logic;
	signal RSTE_up: std_logic;
	signal up_reset: std_logic;
	signal down_reset: std_logic;
	signal P_RSTE: std_logic;
	signal ud_reset: std_logic;
	--
	-- jumpers flipflops
	signal q0_inter: std_logic;
	signal q1_inter: std_logic;
	signal q2_inter: std_logic;
	--
	signal clkn: std_logic;
	
	
BEGIN
	zn <= not z;
	clkn <= not clk;
	
	F <= q(0) and q(1) and q(2) and q(3);
	ZR <= (not q(0)) and (not q(1)) and (not q(2)) and (not q(3));
	SR <= (R and F);
	RSTE_down <= SR;
	
	RSTE_up <= ((not q(0)) and q(1) and (not q(2)) and q(3)) and ud;
	
	up_reset <= (ud and P_RSTE);
	down_reset <= ((not ud) and P_RSTE);
	ud_reset <= (up_reset or down_reset);

	q0_inter <= (q(0) and (not ud)) or (ud and qn(0));
	q1_inter <= (q(1) and (not ud)) or (ud and qn(1));
	q2_inter <= (q(2) and (not ud)) or (ud and qn(2));

	S <= (RSTE_down or RSTE_up) or zn;
	
	ff_d0: dff_vhdl port map(d => qn(0), prs => down_reset, clr => up_reset, clk => clk, q => q(0), qn => qn(0));
	ff_d1: dff_vhdl port map(d => qn(1), prs => '0', clr => ud_reset, clk => q0_inter, q => q(1), qn => qn(1));
	ff_d2: dff_vhdl port map(d => qn(2), prs => '0', clr => ud_reset, clk => q1_inter, q => q(2), qn => qn(2));
	ff_d3: dff_vhdl port map(d => qn(3), prs => down_reset, clr => up_reset, clk => q2_inter, q => q(3), qn => qn(3));
	ff_decode: dff_vhdl port map(d => '0', prs => ZR, clr => SR, clk => '0', q => R, qn => open);
	ff_pulse: dff_vhdl port map(d => '0', prs => S, clr => clkn, clk => '0', q => P_RSTE, qn => open);

	
	co <= ud_reset; 
END TypeArchitecture;
