// Logisim project P10_FUNCIONANDO.circ as structural Verilog
module P0_FFD (
);

  comps comps_1 ();  // open: a

  // Notes on the sheet:
  //   Este bloco de entidade VHDL contém duas entidades VHDL:
  //   A segunda chmada "ffd_vhdl", que será usada em todo este projeto:
  //   A primeira chamada "comps", que será renomeada e que não faz nada:
endmodule

module P1_cnt_mod16_up (
  input  U
);

  wire C, d_ff_1_qn, d_ff_2_q, d_ff_3_q, d_ff_4_qn, d_ff_5_qn, d_ff_6_qn, d_ff_7_q, F_out, FF0_qn, FF1_qn,
       FF2_qn, FF3_qn, nand_1_out, nand_2_out, not_1_out, not_2_out, not_3_out, or_1_out, R_out, Z, ZR_out;
  wire [3:0] cnt_up_down_mod10_vhdl_1_q, d_ff_1_q, FF0_q, multiplexer_1_out;

  Clock clock_1 (.out(C));
  Button #(.press("passive")) u_Z (.out(Z));
  nand nand_1 (nand_1_out, nand_2_out, Z);
  D_Flip_Flop FF0 (.D(FF0_qn), .clk(C), .Q(FF0_q[0]), .Qn(FF0_qn), .reset(d_ff_3_q));  // open: preset
  D_Flip_Flop d_ff_1 (.D(d_ff_1_qn), .clk(C), .Q(d_ff_1_q[0]), .Qn(d_ff_1_qn), .preset(d_ff_2_q));  // open: reset
  D_Flip_Flop d_ff_2 (.Q(d_ff_2_q), .preset(or_1_out), .reset(not_1_out));  // open: D, clk, Qn
  not not_1 (not_1_out, C);
  nand nand_2 (nand_2_out, FF0_q[3], FF0_q[1]);
  D_Flip_Flop d_ff_3 (.Q(d_ff_3_q), .preset(nand_1_out), .reset(not_2_out));  // open: D, clk, Qn
  not not_2 (not_2_out, C);
  D_Flip_Flop FF1 (.D(FF1_qn), .clk(FF0_qn), .Q(FF0_q[1]), .Qn(FF1_qn), .reset(d_ff_3_q));  // open: preset
  D_Flip_Flop d_ff_4 (
    .D(d_ff_4_qn), .clk(d_ff_1_q[0]), .Q(d_ff_1_q[1]), .Qn(d_ff_4_qn), .reset(d_ff_2_q));  // open: preset
  D_Flip_Flop FF2 (.D(FF2_qn), .clk(FF1_qn), .Q(FF0_q[2]), .Qn(FF2_qn), .reset(d_ff_3_q));  // open: preset
  D_Flip_Flop d_ff_5 (
    .D(d_ff_5_qn), .clk(d_ff_1_q[1]), .Q(d_ff_1_q[2]), .Qn(d_ff_5_qn), .reset(d_ff_2_q));  // open: preset
  D_Flip_Flop FF3 (.D(FF3_qn), .clk(FF2_qn), .Q(FF0_q[3]), .Qn(FF3_qn), .reset(d_ff_3_q));  // open: preset
  D_Flip_Flop d_ff_6 (
    .D(d_ff_6_qn), .clk(d_ff_1_q[2]), .Q(d_ff_1_q[3]), .Qn(d_ff_6_qn), .preset(d_ff_2_q));  // open: reset
  Multiplexer #(.width(4)) multiplexer_1 (.in0(FF0_q), .in1(d_ff_1_q), .out(multiplexer_1_out), .sel(U));
  and F (F_out, d_ff_1_q[0], d_ff_1_q[1], d_ff_1_q[2], d_ff_1_q[3]);
  nor ZR (ZR_out, d_ff_1_q[0], d_ff_1_q[1], d_ff_1_q[2], d_ff_1_q[3]);
  D_Flip_Flop d_ff_7 (.Q(d_ff_7_q), .preset(ZR_out), .reset(d_ff_2_q));  // open: D, clk, Qn
  or or_1 (or_1_out, R_out, not_3_out);
  not not_3 (not_3_out, Z);
  Hex_Digit_Display hex_digit_display_1 (.value(multiplexer_1_out));  // open: dp
  and R (R_out, F_out, d_ff_7_q);
  cnt_up_down_mod10_vhdl cnt_up_down_mod10_vhdl_1 (.clk(C), .z(Z), .ud(U), .q(cnt_up_down_mod10_vhdl_1_q));  // open: co
  Hex_Digit_Display hex_digit_display_2 (.value(cnt_up_down_mod10_vhdl_1_q));  // open: dp
endmodule

// VHDL entity comps, as the project stores it:
--------------------------------------------------------------------------------
-- UTFPR - Universidade Tecnológica Federal do Paraná - Curitiba - PR
-- Projeto  : Prática 5 - Cronômetro
-- Circuito : Implementação de um FF tipo D
-- Arquivo  : dff_vhdl.vhd
-- Autor    : prof. Gortan
-- Data     : Outubro 2021
--------------------------------------------------------------------------------
-- Descrição :
-- Implementa um flip-flop tipo D para ser usado como componente em outros circ.
-- obs.: para evitar que o Logisim-evolution 3.6.1 altere o nome do componente
--       introduzimos um componente "comps" no início do arquivo e o ff tipo d
--       vem em segundo lugar - No Quartus ele deve ser comentado / apagado
--------------------------------------------------------------------------------

--============================= Módulo comps: ==================================
library ieee;
  use ieee.std_logic_1164.all;

-- Comentar a entity comps e sua architecture quando usado no Quartus
-- Esse primeira entity é só um artifício para evitar que o Logisim
-- altere o nome do componente ff tipo d, que vem depois
entity comps is
  port(    a  : in  std_logic );
end comps;

architecture cmp_arch of comps is
-- Não faz nada:
begin
end cmp_arch;
-- Fim do trecho a comentar/apagar no Quartus

--==================== Componente: =============================================
library ieee;
  use ieee.std_logic_1164.all;

entity dff_vhdl is
  port(
    d, clk, prs, clr	: in  std_logic;	-- entradas: dado, clk, preset e clear
    q, qn				: out std_logic		-- saídas:   q e q invertido
 );
end dff_vhdl;

architecture ff_d of dff_vhdl is

	signal qstate: std_logic;

begin
	process(clk, clr, prs)
	begin
		if clr = '1' then qstate <= '0';
		elsif prs = '1' then qstate <= '1';
		elsif clk = '1' and clk' event then qstate <= d;
		end if;
	end process;
	q <= qstate;
	qn <= not qstate;
end ff_d;

// VHDL entity cnt_up_down_mod10_vhdl, as the project stores it:
library ieee;
use ieee.std_logic_1164.all;
	
entity cnt_up_down_mod10_vhdl is
	port(
		clk, z, ud	: in  std_logic;					
	    	q       		: out std_logic_vector(3 downto 0);	
	    	co 			: out std_logic
	 );
end cnt_up_down_mod10_vhdl;
	
architecture nt_up_down_mod10_arch of cnt_up_down_mod10_vhdl is
	signal q_up, q_down, qstate_up, qstate_down, qn_up, qn_down: std_logic_vector(3 downto 0);
	signal clk_up, clk_down, clkn_up, clkn_down, rst, zn, reset, ff_rst_in, ff_rst_out, rst_alargador, ff_rst, clr_alargador, clr_aux, prs_rst: std_logic;	
	component dff_vhdl is					-- dff referenciado como dff_vhdl
		port(
			d, clk, prs, clr	: in  std_logic;	-- entradas: dado, clk, preset e clear
			q, qn			: out std_logic 	-- saídas:   q e q invertido
		);
	end component;
begin
	q(0) <= q_up(0) when ud = '0' else q_down(0);
	q(1) <= q_up(1) when ud = '0' else q_down(1);
	q(2) <= q_up(2) when ud = '0' else q_down(2);
	q(3) <= q_up(3) when ud = '0' else q_down(3);
	zn <= not z;
	clk_up <= clk when ud = '0';
	clk_down <= clk when ud = '1';
	clkn_up <= not clk_up;
	clkn_down <= not clk_down;
	prs_rst <= (zn or (qstate_up(1) and qstate_up(3)));
	ff_d0_up: dff_vhdl port map(d => qn_up(0), prs => '0', clr => clr_aux, clk => clk_up,   q => qstate_up(0), qn => qn_up(0));
	ff_d1_up: dff_vhdl port map(d => qn_up(1), prs => '0', clr => clr_aux, clk => qn_up(0), q => qstate_up(1), qn => qn_up(1));
	ff_d2_up: dff_vhdl port map(d => qn_up(2), prs => '0', clr => clr_aux, clk => qn_up(1), q => qstate_up(2), qn => qn_up(2));
	ff_d3_up: dff_vhdl port map(d => qn_up(3), prs => '0', clr => clr_aux, clk => qn_up(2), q => qstate_up(3), qn => qn_up(3));
	ff_rst_up: dff_vhdl port map(d => '0', prs => prs_rst, clr => clkn_up, clk => '0', q => clr_aux);
	q_up(0) <= qstate_up(0);
	q_up(1) <= qstate_up(1);
	q_up(2) <= qstate_up(2);
	q_up(3) <= qstate_up(3);
	reset <= ff_rst_out and (qstate_down(0) and (qstate_down(1) and (qstate_down(2) and qstate_down(3))));
	ff_rst_in <= not (qstate_down(0) or (qstate_down(1) or (qstate_down(2) or qstate_down(3))));
	rst_alargador <= reset or zn;
	ff_d0_down: dff_vhdl port map(d => qn_down(0), prs => rst, clr => '0', clk => clk_down, q => qstate_down(0), qn => qn_down(0));
	ff_d1_down: dff_vhdl port map(d => qn_down(1), prs => '0', clr => ff_rst, clk => qstate_down(0), q => qstate_down(1), qn => qn_down(1));
	ff_d2_down: dff_vhdl port map(d => qn_down(2), prs => '0', clr => ff_rst, clk => qstate_down(1), q => qstate_down(2), qn => qn_down(2));
	ff_d3_down: dff_vhdl port map(d => qn_down(3), prs => rst, clr => '0', clk => qstate_down(2), q => qstate_down(3), qn => qn_down(3));
	ff_rst_down: dff_vhdl port map(d => '0', prs => ff_rst_in, clr => ff_rst, clk => '0', q => ff_rst_out);
	ff_rst_alargador_down: dff_vhdl   port map(d => '0', prs => rst_alargador, clr => clkn_down, clk => '0', q => ff_rst);
	ff_rst_alargador_clr_down: dff_vhdl port map(d => '0', prs => zn, clr => clkn_down, clk => '0', q => clr_alargador);
	rst <= '1' when clr_alargador = '1' else '0';
	q_down(0) <= qstate_down(0);
	q_down(1) <= qstate_down(1);
	q_down(2) <= qstate_down(2);
	q_down(3) <= qstate_down(3);
	co <= clr_aux when ud = '0' else ff_rst;
end nt_up_down_mod10_arch;
