// Logisim project P12_1.circ as structural Verilog
module P0_FFD (
);

  comps comps_1 ();  // open: a

  // Notes on the sheet:
  //   Este bloco de entidade VHDL contém duas entidades VHDL:
  //   A segunda chmada "ffd_vhdl", que será usada em todo este projeto:
  //   A primeira chamada "comps", que será renomeada e que não faz nada:
endmodule

module P1_cnt_mod16_up (
  input  UD
);

  wire and_1_out, CLK_out, cnt_up_down_mod10_1_co, FFT_SST_q, FFT_SST_qn, not_1_out, SST_out, Z_out;
  wire [3:0] cnt_ud_mod6_1_q, cnt_ud_mod60_1_qd, cnt_ud_mod60_1_qu, cnt_up_down_mod10_1_q;

  Button #(.press("passive")) SST (.out(SST_out));
  Clock CLK (.out(CLK_out));
  Button #(.press("passive")) Z (.out(Z_out));
  D_Flip_Flop FFT_SST (
    .D(FFT_SST_qn), .clk(SST_out), .Q(FFT_SST_q), .Qn(FFT_SST_qn), .reset(not_1_out));  // open: preset
  not not_1 (not_1_out, Z_out);
  and and_1 (and_1_out, FFT_SST_q, CLK_out);
  cnt_up_down_mod10 cnt_up_down_mod10_1 (
    .clk(and_1_out), .z(Z_out), .ud(UD), .q(cnt_up_down_mod10_1_q), .co(cnt_up_down_mod10_1_co));
  cnt_ud_mod6 cnt_ud_mod6_1 (.clk(cnt_up_down_mod10_1_co), .z(Z_out), .ud(UD), .q(cnt_ud_mod6_1_q));
  cnt_ud_mod60 cnt_ud_mod60_1 (
    .clk(CLK_out), .z(Z_out), .ud(UD), .sst(SST_out), .qu(cnt_ud_mod60_1_qu), .qd(cnt_ud_mod60_1_qd));
  Hex_Digit_Display hex_digit_display_1 (.value(cnt_ud_mod6_1_q));  // open: dp
  Hex_Digit_Display hex_digit_display_2 (.value(cnt_up_down_mod10_1_q));  // open: dp
  Hex_Digit_Display hex_digit_display_3 (.value(cnt_ud_mod60_1_qd));  // open: dp
  Hex_Digit_Display hex_digit_display_4 (.value(cnt_ud_mod60_1_qu));  // open: dp
endmodule

// VHDL entity comps, as the project stores it:
--------------------------------------------------------------------------------
-- UTFPR - Universidade Tecnológica Federal do Paraná - Curitiba - PR
-- Projeto  : Prática 5 - Cronômetro
-- Circuito : Implementação de um FF tipo D
-- Arquivo  : dff_vhdl.vhd
-- Autor    : prof. Gortan
-- Data     : Outubro 2021
--------------------------------------------------------------------------------
-- Descrição :
-- Implementa um flip-flop tipo D para ser usado como componente em outros circ.
-- obs.: para evitar que o Logisim-evolution 3.6.1 altere o nome do componente
--       introduzimos um componente "comps" no início do arquivo e o ff tipo d
--       vem em segundo lugar - No Quartus ele deve ser comentado / apagado
--------------------------------------------------------------------------------

--============================= Módulo comps: ==================================
library ieee;
  use ieee.std_logic_1164.all;

-- Comentar a entity comps e sua architecture quando usado no Quartus
-- Esse primeira entity é só um artifício para evitar que o Logisim
-- altere o nome do componente ff tipo d, que vem depois
entity comps is
  port(    a  : in  std_logic );
end comps;

architecture cmp_arch of comps is
-- Não faz nada:
begin
end cmp_arch;
-- Fim do trecho a comentar/apagar no Quartus

--==================== Componente: =============================================
library ieee;
  use ieee.std_logic_1164.all;

entity dff_vhdl is
  port(
    d, clk, prs, clr	: in  std_logic;	-- entradas: dado, clk, preset e clear
    q, qn				: out std_logic		-- saídas:   q e q invertido
 );
end dff_vhdl;

architecture ff_d of dff_vhdl is

	signal qstate: std_logic;

begin
	process(clk, clr, prs)
	begin
		if clr = '1' then qstate <= '0';
		elsif prs = '1' then qstate <= '1';
		elsif clk = '1' and clk' event then qstate <= d;
		end if;
	end process;
	q <= qstate;
	qn <= not qstate;
end ff_d;

// VHDL entity cnt_up_down_mod10, as the project stores it:
LIBRARY ieee;
USE ieee.std_logic_1164.all;

ENTITY cnt_up_down_mod10 IS
  PORT (
    	clk, z, ud  : in  std_logic;					-- entradas clk, rst
    	q       : inout std_logic_vector(3 downto 0);	-- saída q3 até q0
	co : out std_logic
    );
END cnt_up_down_mod10;

--------------------------------------------------------------------------------
--Complete your VHDL description below
--------------------------------------------------------------------------------

ARCHITECTURE TypeArchitecture OF cnt_up_down_mod10 IS

	signal zn: std_logic;
	signal qn: std_logic_vector(3 downto 0);	-- liga qn com d
	
	component dff_vhdl is					-- dff referenciado como dff_vhdl
		port
		(
			d, clk, prs, clr	: in  std_logic;	-- entradas: dado, clk, preset e clear
			q, qn			: out std_logic 	-- saídas:   q e q invertido
		);
	end component;
	-- decodificardor
	signal F: std_logic;
	signal ZR: std_logic;
	signal SR: std_logic;
	signal R: std_logic;
	signal S: std_logic;
	--
	-- pulsos reset
	signal RSTE_down: std_logic;
	signal RSTE_up: std_logic;
	signal up_reset: std_logic;
	signal down_reset: std_logic;
	signal P_RSTE: std_logic;
	signal ud_reset: std_logic;
	--
	-- jumpers flipflops
	signal q0_inter: std_logic;
	signal q1_inter: std_logic;
	signal q2_inter: std_logic;
	--
	signal clkn: std_logic;
	
	
BEGIN
	zn <= not z;
	clkn <= not clk;
	
	F <= q(0) and q(1) and q(2) and q(3);
	ZR <= (not q(0)) and (not q(1)) and (not q(2)) and (not q(3));
	SR <= (R and F);
	RSTE_down <= SR;
	
	RSTE_up <= ((not q(0)) and q(1) and (not q(2)) and q(3)) and ud;
	
	up_reset <= (ud and P_RSTE);
	down_reset <= ((not ud) and P_RSTE);
	ud_reset <= (up_reset or down_reset);

	q0_inter <= (q(0) and (not ud)) or (ud and qn(0));
	q1_inter <= (q(1) and (not ud)) or (ud and qn(1));
	q2_inter <= (q(2) and (not ud)) or (ud and qn(2));

	S <= (RSTE_down or RSTE_up) or zn;
	
	ff_d0: dff_vhdl port map(d => qn(0), prs => down_reset, clr => up_reset, clk => clk, q => q(0), qn => qn(0));
	ff_d1: dff_vhdl port map(d => qn(1), prs => '0', clr => ud_reset, clk => q0_inter, q => q(1), qn => qn(1));
	ff_d2: dff_vhdl port map(d => qn(2), prs => '0', clr => ud_reset, clk => q1_inter, q => q(2), qn => qn(2));
	ff_d3: dff_vhdl port map(d => qn(3), prs => down_reset, clr => up_reset, clk => q2_inter, q => q(3), qn => qn(3));
	ff_decode: dff_vhdl port map(d => '0', prs => ZR, clr => SR, clk => '0', q => R, qn => open);
	ff_pulse: dff_vhdl port map(d => '0', prs => S, clr => clkn, clk => '0', q => P_RSTE, qn => open);

	
	co <= ud_reset; 
END TypeArchitecture;

// VHDL entity cnt_ud_mod60, as the project stores it:
LIBRARY ieee;
USE ieee.std_logic_1164.all;

ENTITY cnt_ud_mod60 IS
  PORT (
    	clk, z, ud,  sst  : in  std_logic;					-- entradas clk, rst
    	qu, qd       : inout std_logic_vector(3 downto 0)	-- saída q3 até q0
    );
END cnt_ud_mod60;

--------------------------------------------------------------------------------
--Complete your VHDL description below
--------------------------------------------------------------------------------

ARCHITECTURE TypeArchitecture OF cnt_ud_mod60 IS

	signal zn: std_logic;
	signal qnu: std_logic_vector(3 downto 0);	-- liga qn com d
	signal qnd: std_logic_vector(3 downto 0);

	component dff_vhdl is					-- dff referenciado como dff_vhdl
		port
		(
			d, clk, prs, clr	: in  std_logic;	-- entradas: dado, clk, preset e clear
			q, qn			: out std_logic 	-- saídas:   q e q invertido
		);
	end component;

-- SST

	signal q_sst : std_logic;
	signal qn_sst : std_logic;
	signal clksst: std_logic;
-- MOD10
		-- decodificardor
	signal Fu: std_logic;
	signal ZRu: std_logic;
	signal SRu: std_logic;
	signal Ru: std_logic;
	signal Su: std_logic;
	--
	-- pulsos reset
	signal RSTE_downu: std_logic;
	signal RSTE_upu: std_logic;
	signal up_resetu: std_logic;
	signal down_resetu: std_logic;
	signal P_RSTEu: std_logic;
	signal ud_resetu: std_logic;
	--
	-- jumpers flipflops
	signal q0_interu: std_logic;
	signal q1_interu: std_logic;
	signal q2_interu: std_logic;
	--
	signal clknu: std_logic;
	signal co: std_logic;


	-- MOD 6
	-- decodificardor
	signal Fd: std_logic;
	signal ZRd: std_logic;
	signal SRd: std_logic;
	signal Rd: std_logic;
	signal Sd: std_logic;
	--
	-- pulsos reset
	signal RSTE_downd: std_logic;
	signal RSTE_upd: std_logic;
	signal up_resetd: std_logic;
	signal down_resetd: std_logic;
	signal P_RSTEd: std_logic;
	signal ud_resetd: std_logic;
	--
	-- jumpers flipflops
	signal q0_interd: std_logic;
	signal q1_interd: std_logic;
	--
	signal clknd: std_logic;
BEGIN

	zn <= not z;
	ff_sst: dff_vhdl port map(d=> qn_sst, prs => '0', clr => zn, clk => sst, q=> q_sst, qn=> qn_sst);
	clksst <= q_sst and clk;
-- mod 10

	clknu <= not clk;
	
	Fu <= qu(0) and qu(1) and qu(2) and qu(3);
	ZRu <= (not qu(0)) and (not qu(1)) and (not qu(2)) and (not qu(3));
	SRu <= (Ru and Fu);
	RSTE_downu <= SRu;
	
	RSTE_upu <= ((not qu(0)) and qu(1) and (not qu(2)) and qu(3)) and ud;
	
	up_resetu <= (ud and P_RSTEu);
	down_resetu <= ((not ud) and P_RSTEu);
	ud_resetu <= (up_resetu or down_resetu);

	q0_interu <= (qu(0) and (not ud)) or (ud and qnu(0));
	q1_interu <= (qu(1) and (not ud)) or (ud and qnu(1));
	q2_interu <= (qu(2) and (not ud)) or (ud and qnu(2));

	Su <= (RSTE_downu or RSTE_upu) or zn;
	
	ff_d0u: dff_vhdl port map(d => qnu(0), prs => down_resetu, clr => up_resetu, clk => clksst, q => qu(0), qn => qnu(0));
	ff_d1u: dff_vhdl port map(d => qnu(1), prs => '0', clr => ud_resetu, clk => q0_interu, q => qu(1), qn => qnu(1));
	ff_d2u: dff_vhdl port map(d => qnu(2), prs => '0', clr => ud_resetu, clk => q1_interu, q => qu(2), qn => qnu(2));
	ff_d3u: dff_vhdl port map(d => qnu(3), prs => down_resetu, clr => up_resetu, clk => q2_interu, q => qu(3), qn => qnu(3));
	ff_decodeu: dff_vhdl port map(d => '0', prs => ZRu, clr => SRu, clk => '0', q => Ru, qn => open);
	ff_pulseu: dff_vhdl port map(d => '0', prs => Su, clr => clknu, clk => '0', q => P_RSTEu, qn => open);
	
	co <= ud_resetu;

-- MOD 6


	qd(3) <= '0';
	clknd <= not co;
	
	Fd <= qd(0) and qd(1) and qd(2);
	ZRd <= (not qd(0)) and (not qd(1)) and (not qd(2));
	SRd <= (Rd and Fd);
	RSTE_downd <= SRd;
	
	RSTE_upd <= ((not qd(0)) and qd(1) and  qd(2)) and ud;
	
	up_resetd <= (ud and P_RSTEd);
	down_resetd <= ((not ud) and P_RSTEd);
	ud_resetd <= (up_resetd or down_resetd);

	q0_interd <= (qd(0) and (not ud)) or (ud and qnd(0));
	q1_interd <= (qd(1) and (not ud)) or (ud and qnd(1));


	Sd <= (RSTE_downd or RSTE_upd) or zn;
	
	ff_d0d: dff_vhdl port map(d => qnd(0), prs => down_resetd, clr => up_resetd, clk => co, q => qd(0), qn => qnd(0));
	ff_d1d: dff_vhdl port map(d => qnd(1), prs => '0', clr => ud_resetd, clk => q0_interd, q => qd(1), qn => qnd(1));
	ff_d2d: dff_vhdl port map(d => qnd(2), prs => down_resetd, clr => up_resetd, clk => q1_interd, q => qd(2), qn => qnd(2));
	ff_decoded: dff_vhdl port map(d => '0', prs => ZRd, clr => SRd, clk => '0', q => Rd, qn => open);
	ff_pulsed: dff_vhdl port map(d => '0', prs => Sd, clr => clknd, clk => '0', q => P_RSTEd, qn => open);
	

END TypeArchitecture;

// VHDL entity cnt_ud_mod6, as the project stores it:
LIBRARY ieee;
USE ieee.std_logic_1164.all;

ENTITY cnt_ud_mod6 IS
  PORT (
    clk, z, ud  : in  std_logic;					-- entradas clk, rst
    q       : inout std_logic_vector(3 downto 0)	-- saída q3 até q0
    );
END cnt_ud_mod6;

--------------------------------------------------------------------------------
--Complete your VHDL description below
--------------------------------------------------------------------------------

ARCHITECTURE TypeArchitecture OF cnt_ud_mod6 IS

	signal zn: std_logic;
	signal qn: std_logic_vector(3 downto 0);	-- liga qn com d
	
	component dff_vhdl is					-- dff referenciado como dff_vhdl
		port
		(
			d, clk, prs, clr	: in  std_logic;	-- entradas: dado, clk, preset e clear
			q, qn			: out std_logic 	-- saídas:   q e q invertido
		);
	end component;
	-- decodificardor
	signal F: std_logic;
	signal ZR: std_logic;
	signal SR: std_logic;
	signal R: std_logic;
	signal S: std_logic;
	--
	-- pulsos reset
	signal RSTE_down: std_logic;
	signal RSTE_up: std_logic;
	signal up_reset: std_logic;
	signal down_reset: std_logic;
	signal P_RSTE: std_logic;
	signal ud_reset: std_logic;
	--
	-- jumpers flipflops
	signal q0_inter: std_logic;
	signal q1_inter: std_logic;
	--
	signal clkn: std_logic;
BEGIN
	q(3) <= '0';
	zn <= not z;
	clkn <= not clk;
	
	F <= q(0) and q(1) and q(2);
	ZR <= (not q(0)) and (not q(1)) and (not q(2));
	SR <= (R and F);
	RSTE_down <= SR;
	
	RSTE_up <= ((not q(0)) and q(1) and  q(2)) and ud;
	
	up_reset <= (ud and P_RSTE);
	down_reset <= ((not ud) and P_RSTE);
	ud_reset <= (up_reset or down_reset);

	q0_inter <= (q(0) and (not ud)) or (ud and qn(0));
	q1_inter <= (q(1) and (not ud)) or (ud and qn(1));


	S <= (RSTE_down or RSTE_up) or zn;
	
	ff_d0: dff_vhdl port map(d => qn(0), prs => down_reset, clr => up_reset, clk => clk, q => q(0), qn => qn(0));
	ff_d1: dff_vhdl port map(d => qn(1), prs => '0', clr => ud_reset, clk => q0_inter, q => q(1), qn => qn(1));
	ff_d2: dff_vhdl port map(d => qn(2), prs => down_reset, clr => up_reset, clk => q1_inter, q => q(2), qn => qn(2));
	ff_decode: dff_vhdl port map(d => '0', prs => ZR, clr => SR, clk => '0', q => R, qn => open);
	ff_pulse: dff_vhdl port map(d => '0', prs => S, clr => clkn, clk => '0', q => P_RSTE, qn => open);

END TypeArchitecture;
