// Logisim project P12_3.circ as structural Verilog
module P0_FFD (
);

  comps comps_1 ();  // open: a

  // Notes on the sheet:
  //   Este bloco de entidade VHDL contém duas entidades VHDL:
  //   A segunda chmada "ffd_vhdl", que será usada em todo este projeto:
  //   A primeira chamada "comps", que será renomeada e que não faz nada:
endmodule

module P1_cnt_mod16_up (
  input  UD
);

  wire and_1_out, CLK_out, cnt_up_down_mod10_vhdl_1_co, FFT_SST_q, FFT_SST_qn, not_1_out, SST_out, Z_out;
  wire [3:0] cnt_up_down_mod6_vhdl_1_q, cnt_up_down_mod10_vhdl_1_q, cnt_up_down_mod60_vhdl_1_qd,
       cnt_up_down_mod60_vhdl_1_qu;

  Button #(.press("passive")) SST (.out(SST_out));
  Clock CLK (.out(CLK_out));
  Button #(.press("passive")) Z (.out(Z_out));
  D_Flip_Flop FFT_SST (
    .D(FFT_SST_qn), .clk(SST_out), .Q(FFT_SST_q), .Qn(FFT_SST_qn), .reset(not_1_out));  // open: preset
  not not_1 (not_1_out, Z_out);
  and and_1 (and_1_out, FFT_SST_q, CLK_out);
  cnt_up_down_mod10_vhdl cnt_up_down_mod10_vhdl_1 (
    .clk(and_1_out), .z(Z_out), .ud(UD), .q(cnt_up_down_mod10_vhdl_1_q), .co(cnt_up_down_mod10_vhdl_1_co));
  cnt_up_down_mod6_vhdl cnt_up_down_mod6_vhdl_1 (
    .clk(cnt_up_down_mod10_vhdl_1_co), .z(Z_out), .ud(UD), .q(cnt_up_down_mod6_vhdl_1_q));
  cnt_up_down_mod60_vhdl cnt_up_down_mod60_vhdl_1 (
    .clk(CLK_out), .z(Z_out), .ud(UD), .sst(SST_out), .qu(cnt_up_down_mod60_vhdl_1_qu),
    .qd(cnt_up_down_mod60_vhdl_1_qd));
  Hex_Digit_Display hex_digit_display_1 (.value(cnt_up_down_mod6_vhdl_1_q));  // open: dp
  Hex_Digit_Display hex_digit_display_2 (.value(cnt_up_down_mod10_vhdl_1_q));  // open: dp
  Hex_Digit_Display hex_digit_display_3 (.value(cnt_up_down_mod60_vhdl_1_qd));  // open: dp
  Hex_Digit_Display hex_digit_display_4 (.value(cnt_up_down_mod60_vhdl_1_qu));  // open: dp
endmodule

// VHDL entity comps, as the project stores it:
--------------------------------------------------------------------------------
-- UTFPR - Universidade Tecnológica Federal do Paraná - Curitiba - PR
-- Projeto  : Prática 5 - Cronômetro
-- Circuito : Implementação de um FF tipo D
-- Arquivo  : dff_vhdl.vhd
-- Autor    : prof. Gortan
-- Data     : Outubro 2021
--------------------------------------------------------------------------------
-- Descrição :
-- Implementa um flip-flop tipo D para ser usado como componente em outros circ.
-- obs.: para evitar que o Logisim-evolution 3.6.1 altere o nome do componente
--       introduzimos um componente "comps" no início do arquivo e o ff tipo d
--       vem em segundo lugar - No Quartus ele deve ser comentado / apagado
--------------------------------------------------------------------------------

--============================= Módulo comps: ==================================
library ieee;
  use ieee.std_logic_1164.all;

-- Comentar a entity comps e sua architecture quando usado no Quartus
-- Esse primeira entity é só um artifício para evitar que o Logisim
-- altere o nome do componente ff tipo d, que vem depois
entity comps is
  port(    a  : in  std_logic );
end comps;

architecture cmp_arch of comps is
-- Não faz nada:
begin
end cmp_arch;
-- Fim do trecho a comentar/apagar no Quartus

--==================== Componente: =============================================
library ieee;
  use ieee.std_logic_1164.all;

entity dff_vhdl is
  port(
    d, clk, prs, clr	: in  std_logic;	-- entradas: dado, clk, preset e clear
    q, qn				: out std_logic		-- saídas:   q e q invertido
 );
end dff_vhdl;

architecture ff_d of dff_vhdl is

	signal qstate: std_logic;

begin
	process(clk, clr, prs)
	begin
		if clr = '1' then qstate <= '0';
		elsif prs = '1' then qstate <= '1';
		elsif clk = '1' and clk' event then qstate <= d;
		end if;
	end process;
	q <= qstate;
	qn <= not qstate;
end ff_d;

// VHDL entity cnt_up_down_mod10_vhdl, as the project stores it:
library ieee;
use ieee.std_logic_1164.all;
	
entity cnt_up_down_mod10_vhdl is
    port(
        clk, z, ud  : in  std_logic;                    
        q           : out std_logic_vector(3 downto 0); 
        co          : out std_logic
     );
end cnt_up_down_mod10_vhdl;
	
architecture nt_up_down_mod10_arch of cnt_up_down_mod10_vhdl is
	signal q_up, q_down, qstate_up, qstate_down, qn_up, qn_down: std_logic_vector(3 downto 0);
	signal clk_up, clk_down, clkn_up, clkn_down, rst, zn, reset, ff_rst_in, ff_rst_out, rst_alargador, ff_rst, clr_alargador, clr_aux, prs_rst: std_logic;	
	component dff_vhdl is
		port(
			d, clk, prs, clr	: in  std_logic;
			q, qn			: out std_logic
		);
	end component;
begin
	q(0) <= q_up(0) when ud = '0' else q_down(0);
	q(1) <= q_up(1) when ud = '0' else q_down(1);
	q(2) <= q_up(2) when ud = '0' else q_down(2);
	q(3) <= q_up(3) when ud = '0' else q_down(3);
	zn <= not z;
	clk_up <= clk when ud = '0' else '0';
	clk_down <= clk when ud = '1' else '0';
	clkn_up <= not clk_up;
	clkn_down <= not clk_down;
	prs_rst <= (zn or (qstate_up(1) and qstate_up(3)));
	ff_d0_up: dff_vhdl port map(d => qn_up(0), prs => '0', clr => clr_aux, clk => clk_up,   q => qstate_up(0), qn => qn_up(0));
	ff_d1_up: dff_vhdl port map(d => qn_up(1), prs => '0', clr => clr_aux, clk => qn_up(0), q => qstate_up(1), qn => qn_up(1));
	ff_d2_up: dff_vhdl port map(d => qn_up(2), prs => '0', clr => clr_aux, clk => qn_up(1), q => qstate_up(2), qn => qn_up(2));
	ff_d3_up: dff_vhdl port map(d => qn_up(3), prs => '0', clr => clr_aux, clk => qn_up(2), q => qstate_up(3), qn => qn_up(3));
	ff_rst_up: dff_vhdl port map(d => '0', prs => prs_rst, clr => clkn_up, clk => '0', q => clr_aux);
	q_up(0) <= qstate_up(0);
	q_up(1) <= qstate_up(1);
	q_up(2) <= qstate_up(2);
	q_up(3) <= qstate_up(3);

  
	reset <= ff_rst_out and (qstate_down(0) and qstate_down(1) and qstate_down(2) and qstate_down(3));
	ff_rst_in <= not (qstate_down(0) or qstate_down(1) or qstate_down(2) or qstate_down(3));
   

	rst_alargador <= reset or zn;
	ff_d0_down: dff_vhdl port map(d => qn_down(0), prs => rst, clr => '0', clk => clk_down, q => qstate_down(0), qn => qn_down(0));
	ff_d1_down: dff_vhdl port map(d => qn_down(1), prs => '0', clr => ff_rst, clk => qstate_down(0), q => qstate_down(1), qn => qn_down(1));
	ff_d2_down: dff_vhdl port map(d => qn_down(2), prs => '0', clr => ff_rst, clk => qstate_down(1), q => qstate_down(2), qn => qn_down(2));
	ff_d3_down: dff_vhdl port map(d => qn_down(3), prs => rst, clr => '0', clk => qstate_down(2), q => qstate_down(3), qn => qn_down(3));
	ff_rst_down: dff_vhdl port map(d => '0', prs => ff_rst_in, clr => ff_rst, clk => '0', q => ff_rst_out);
	ff_rst_alargador_down: dff_vhdl    port map(d => '0', prs => rst_alargador, clr => clkn_down, clk => '0', q => ff_rst);
	ff_rst_alargador_clr_down: dff_vhdl port map(d => '0', prs => rst_alargador, clr => clkn_down, clk => '0', q => clr_alargador);

	rst <= '1' when clr_alargador = '1' else '0';
	q_down(0) <= qstate_down(0);
	q_down(1) <= qstate_down(1);
	q_down(2) <= qstate_down(2);
	q_down(3) <= qstate_down(3);
	co <= clr_aux when ud = '0' else ff_rst;
end nt_up_down_mod10_arch;

// VHDL entity cnt_up_down_mod6_vhdl, as the project stores it:
library ieee;
use ieee.std_logic_1164.all;

entity cnt_up_down_mod6_vhdl is
	port(
    		clk, z, ud	: in  std_logic;					
    		q       		: out std_logic_vector(3 downto 0)	
	 );
end cnt_up_down_mod6_vhdl;

architecture P12_cnt_up_down_mod6_arch of cnt_up_down_mod6_vhdl is
	signal q_up, q_down, qstate_up, qstate_down, qn_up, qn_down: std_logic_vector(3 downto 0);
	signal clk_up, clk_down, clkn_up, clkn_down, rst, zn, reset, ff_rst_in, ff_rst_out, rst_alargador, ff_rst, clr_alargador, clr_aux, prs_rst: std_logic;
	component dff_vhdl is					
		port(
			d, clk, prs, clr	: in  std_logic;	
			q, qn			: out std_logic
		);
	end component;
begin
	q(0) <= q_up(0) when ud = '0' else q_down(0);
	q(1) <= q_up(1) when ud = '0' else q_down(1);
	q(2) <= q_up(2) when ud = '0' else q_down(2);
	q(3) <= q_up(3) when ud = '0' else q_down(3);
	zn <= not z;
	clk_up <= clk when ud = '0';
	clk_down <= clk when ud = '1';
	clkn_up <= not clk_up;
	clkn_down <= not clk_down;
	prs_rst <= (zn or (qstate_up(1) and qstate_up(2)));
	ff_d0_up:  dff_vhdl port map(d => qn_up(0), prs => '0',     clr => clr_aux, clk => clk_up,   q => qstate_up(0), qn => qn_up(0));
	ff_d1_up:  dff_vhdl port map(d => qn_up(1), prs => '0',     clr => clr_aux, clk => qn_up(0), q => qstate_up(1), qn => qn_up(1));
	ff_d2_up:  dff_vhdl port map(d => qn_up(2), prs => '0',     clr => clr_aux, clk => qn_up(1), q => qstate_up(2), qn => qn_up(2));
	ff_d3_up:  dff_vhdl port map(d => qn_up(3), prs => '0',     clr => clr_aux, clk => qn_up(2), q => qstate_up(3), qn => qn_up(3));
	ff_rst_up: dff_vhdl port map(d => '0',      prs => prs_rst, clr => clkn_up, clk => '0',      q => clr_aux);
	q_up(0) <= qstate_up(0);
	q_up(1) <= qstate_up(1);
	q_up(2) <= qstate_up(2);
	q_up(3) <= qstate_up(3);
	reset <= (qstate_down(0) and (qstate_down(1) and (qstate_down(2) and qstate_down(3))));
	rst_alargador <= reset or zn;
	ff_d0_down: dff_vhdl port map(d => qn_down(0), prs => rst, clr => '0',    clk => clk_down,       q => qstate_down(0), qn => qn_down(0));
	ff_d1_down: dff_vhdl port map(d => qn_down(1), prs => '0', clr => ff_rst, clk => qstate_down(0), q => qstate_down(1), qn => qn_down(1));
	ff_d2_down: dff_vhdl port map(d => qn_down(2), prs => rst, clr => '0', clk => qstate_down(1), q => qstate_down(2), qn => qn_down(2));
	ff_d3_down: dff_vhdl port map(d => qn_down(3), prs => '0', clr => ff_rst,    clk => qstate_down(2), q => qstate_down(3), qn => qn_down(3));
	ff_rst_alargador_down: dff_vhdl port map(d => '0', prs => rst_alargador, clr => clkn_down, clk => '0', q => ff_rst);
	ff_rst_clr_alargador_down: dff_vhdl port map(d => '0', prs => zn, clr => clkn_down, clk => '0', q => clr_alargador);
	rst <= '1' when clr_alargador = '1' else '0';
	q_down(0) <= qstate_down(0);
	q_down(1) <= qstate_down(1);
	q_down(2) <= qstate_down(2);
	q_down(3) <= qstate_down(3);
end P12_cnt_up_down_mod6_arch;

// VHDL entity cnt_up_down_mod60_vhdl, as the project stores it:
library ieee;
use ieee.std_logic_1164.all;

entity cnt_up_down_mod60_vhdl is
    port(
        clk, z, ud, sst : in  std_logic;
        qu, qd          : out std_logic_vector(3 downto 0)
    );
end cnt_up_down_mod60_vhdl;

architecture cnt_up_down_mod60_arch of cnt_up_down_mod60_vhdl is

    -- Sinais Bloco Mod-10
    signal ff_rst_in, ff_rst_out, qo : std_logic;
    signal q_up_m10, q_down_m10, qstate_up_m10, qstate_down_m10, qn_up_m10, qn_down_m10 : std_logic_vector(3 downto 0);
    signal clk_up_m10, clk_down_m10, clkn_up_m10, clkn_down_m10, rst_m10, zn_m10, reset_m10, rst_alargador_m10, ff_rst_m10, clr_alargador_m10, clr_aux_m10, prs_rst_m10 : std_logic;
    
    -- Sinais Bloco Mod-6
    signal q_up_m6, q_down_m6, qstate_up_m6, qstate_down_m6, qn_up_m6, qn_down_m6 : std_logic_vector(3 downto 0);
    signal clk_up_m6, clk_down_m6, clkn_up_m6, clkn_down_m6, rst_m6, zn_m6, reset_m6, rst_alargador_m6, ff_rst_m6, clr_alargador_m6, clr_aux_m6, prs_rst_m6 : std_logic;
    signal ff_rst_in_m6, ff_rst_out_m6 : std_logic; 

    -- Sinal de clock "habilitado"
    signal clk_gated : std_logic;

    component dff_vhdl is
        port(
            d, clk, prs, clr : in  std_logic;
            q, qn            : out std_logic
        );
    end component;

begin
    ---------------------------------------------------------
    -- START/STOP (P13) - LÓGICA DE HABILITAÇÃO
    ---------------------------------------------------------
    clk_gated <= clk and sst;

    ---------------------------------------------------------
    -- BLOCO MOD10 (Unidades)
    ---------------------------------------------------------
    qu(0) <= q_up_m10(0) when ud = '0' else q_down_m10(0);
    qu(1) <= q_up_m10(1) when ud = '0' else q_down_m10(1);
    qu(2) <= q_up_m10(2) when ud = '0' else q_down_m10(2);
    qu(3) <= q_up_m10(3) when ud = '0' else q_down_m10(3);

    zn_m10 <= not z; -- z é ativo-alto do debouncer
    clk_up_m10 <= clk_gated when ud = '0' else '0'; 
    clk_down_m10 <= clk_gated when ud = '1' else '0'; 
    clkn_up_m10 <= not clk_up_m10;
    clkn_down_m10 <= not clk_down_m10;
    
    prs_rst_m10 <= (zn_m10 or (qstate_up_m10(1) and qstate_up_m10(3))); -- Detecta 10 (1010)

    ff_d0_up_m10: dff_vhdl port map(d => qn_up_m10(0), prs => '0', clr => clr_aux_m10, clk => clk_up_m10, q => qstate_up_m10(0), qn => qn_up_m10(0));
    ff_d1_up_m10: dff_vhdl port map(d => qn_up_m10(1), prs => '0', clr => clr_aux_m10, clk => qn_up_m10(0), q => qstate_up_m10(1), qn => qn_up_m10(1));
    ff_d2_up_m10: dff_vhdl port map(d => qn_up_m10(2), prs => '0', clr => clr_aux_m10, clk => qn_up_m10(1), q => qstate_up_m10(2), qn => qn_up_m10(2));
    ff_d3_up_m10: dff_vhdl port map(d => qn_up_m10(3), prs => '0', clr => clr_aux_m10, clk => qn_up_m10(2), q => qstate_up_m10(3), qn => qn_up_m10(3));
    ff_rst_up_m10: dff_vhdl port map(d => '0', prs => prs_rst_m10, clr => clkn_up_m10, clk => '0', q => clr_aux_m10);

    q_up_m10(0) <= qstate_up_m10(0);
    q_up_m10(1) <= qstate_up_m10(1);
    q_up_m10(2) <= qstate_up_m10(2);
    q_up_m10(3) <= qstate_up_m10(3);

    -- Lógica Regressiva (DOWN) Mod-10
    reset_m10 <= ff_rst_out and (qstate_down_m10(0) and qstate_down_m10(1) and qstate_down_m10(2) and qstate_down_m10(3)); -- Detecta 15 (1111)
    ff_rst_in <= not (qstate_down_m10(0) or qstate_down_m10(1) or qstate_down_m10(2) or qstate_down_m10(3)); -- Detecta 0 (0000)
    rst_alargador_m10 <= reset_m10 or zn_m10;

    ff_d0_down_m10: dff_vhdl port map(d => qn_down_m10(0), prs => rst_m10, clr => '0', clk => clk_down_m10, q => qstate_down_m10(0), qn => qn_down_m10(0));
    ff_d1_down_m10: dff_vhdl port map(d => qn_down_m10(1), prs => '0', clr => ff_rst_m10, clk => qstate_down_m10(0), q => qstate_down_m10(1), qn => qn_down_m10(1));
    ff_d2_down_m10: dff_vhdl port map(d => qn_down_m10(2), prs => '0', clr => ff_rst_m10, clk => qstate_down_m10(1), q => qstate_down_m10(2), qn => qn_down_m10(2));
    ff_d3_down_m10: dff_vhdl port map(d => qn_down_m10(3), prs => rst_m10, clr => '0', clk => qstate_down_m10(2), q => qstate_down_m10(3), qn => qn_down_m10(3));

    ff_rst_down_m10: dff_vhdl port map(d => '0', prs => ff_rst_in, clr => ff_rst_m10, clk => '0', q => ff_rst_out);
    ff_rst_alargador_down_m10: dff_vhdl port map(d => '0', prs => rst_alargador_m10, clr => clkn_down_m10, clk => '0', q => ff_rst_m10);
    ff_rst_alargador_clr_down_m10: dff_vhdl port map(d => '0', prs => rst_alargador_m10, clr => clkn_down_m10, clk => '0', q => clr_alargador_m10);
    
    rst_m10 <= '1' when clr_alargador_m10 = '1' else '0';
    q_down_m10(0) <= qstate_down_m10(0);
    q_down_m10(1) <= qstate_down_m10(1);
    q_down_m10(2) <= qstate_down_m10(2);
    q_down_m10(3) <= qstate_down_m10(3);

    qo <= clr_aux_m10 when ud = '0' else ff_rst_m10;

    ---------------------------------------------------------
    -- BLOCO MOD6 (Dezenas)
    ---------------------------------------------------------
    qd(0) <= q_up_m6(0) when ud = '0' else q_down_m6(0);
    qd(1) <= q_up_m6(1) when ud = '0' else q_down_m6(1);
    qd(2) <= q_up_m6(2) when ud = '0' else q_down_m6(2);
    qd(3) <= q_up_m6(3) when ud = '0' else q_down_m6(3);

    zn_m6 <= not z;
    clk_up_m6 <= qo when ud = '0' else '0';
    clk_down_m6 <= qo when ud = '1' else '0';
    clkn_up_m6 <= not clk_up_m6;
    clkn_down_m6 <= not clk_down_m6;

    prs_rst_m6 <= (zn_m6 or (qstate_up_m6(1) and qstate_up_m6(2))); -- Detecta 6 (0110)

    ff_d0_up_m6: dff_vhdl port map(d => qn_up_m6(0), prs => '0', clr => clr_aux_m6, clk => clk_up_m6,   q => qstate_up_m6(0), qn => qn_up_m6(0));
    ff_d1_up_m6: dff_vhdl port map(d => qn_up_m6(1), prs => '0', clr => clr_aux_m6, clk => qn_up_m6(0), q => qstate_up_m6(1), qn => qn_up_m6(1));
    ff_d2_up_m6: dff_vhdl port map(d => qn_up_m6(2), prs => '0', clr => clr_aux_m6, clk => qn_up_m6(1), q => qstate_up_m6(2), qn => qn_up_m6(2));
    ff_d3_up_m6: dff_vhdl port map(d => qn_up_m6(3), prs => '0', clr => clr_aux_m6, clk => qn_up_m6(2), q => qstate_up_m6(3), qn => qn_up_m6(3));
    
    ff_rst_up_m6: dff_vhdl port map(d => '0', prs => prs_rst_m6, clr => clkn_up_m6, clk => '0', q => clr_aux_m6);
    q_up_m6(0) <= qstate_up_m6(0);
    q_up_m6(1) <= qstate_up_m6(1);
    q_up_m6(2) <= qstate_up_m6(2);
    q_up_m6(3) <= qstate_up_m6(3);
    
    -- Lógica Regressiva (DOWN) Mod-6 (CORREÇÃO P12)
    ff_rst_in_m6 <= not (qstate_down_m6(0) or qstate_down_m6(1) or qstate_down_m6(2) or qstate_down_m6(3));
    ff_rst_down_m6: dff_vhdl port map(d => '0', prs => ff_rst_in_m6, clr => ff_rst_m6, clk => '0', q => ff_rst_out_m6);

    reset_m6 <= ff_rst_out_m6 and (not qstate_down_m6(3)) and qstate_down_m6(2) and qstate_down_m6(1) and qstate_down_m6(0); -- Detecta 7 (0111)
    
    rst_alargador_m6 <= reset_m6 or zn_m6;

    ff_d0_down_m6: dff_vhdl port map(d => qn_down_m6(0), prs => rst_m6, clr => '0', clk => clk_down_m6, q => qstate_down_m6(0), qn => qn_down_m6(0));
    ff_d1_down_m6: dff_vhdl port map(d => qn_down_m6(1), prs => '0', clr => ff_rst_m6, clk => qstate_down_m6(0), q => qstate_down_m6(1), qn => qn_down_m6(1));
    ff_d2_down_m6: dff_vhdl port map(d => qn_down_m6(2), prs => rst_m6, clr => '0', clk => qstate_down_m6(1), q => qstate_down_m6(2), qn => qn_down_m6(2));
    ff_d3_down_m6: dff_vhdl port map(d => qn_down_m6(3), prs => '0', clr => ff_rst_m6, clk => qstate_down_m6(2), q => qstate_down_m6(3), qn => qn_down_m6(3));

    ff_rst_alargador_down_m6: dff_vhdl port map(d => '0', prs => rst_alargador_m6, clr => clkn_down_m6, clk => '0', q => ff_rst_m6);
    ff_rst_alargador_clr_down_m6: dff_vhdl port map(d => '0', prs => rst_alargador_m6, clr => clkn_down_m6, clk => '0', q => clr_alargador_m6);

    rst_m6 <= '1' when clr_alargador_m6 = '1' else '0';
    q_down_m6(0) <= qstate_down_m6(0);
    q_down_m6(1) <= qstate_down_m6(1);
    q_down_m6(2) <= qstate_down_m6(2);
    q_down_m6(3) <= qstate_down_m6(3);
    
end cnt_up_down_mod60_arch;
