// Logisim project P2_funcionando.circ as structural Verilog
module P0_FFD (
);

  comps comps_1 ();  // open: a

  // Notes on the sheet:
  //   Este bloco de entidade VHDL contém duas entidades VHDL:
  //   A segunda chmada "ffd_vhdl", que será usada em todo este projeto:
  //   A primeira chamada "comps", que será renomeada e que não faz nada:
endmodule

module P1_cnt_mod16_up (
);

  wire and_1_out, and_2_out, C, FF0_qn, FF1_qn, FF2_qn, FF3_qn, not_1_out, not_2_out, not_3_out, not_4_out,
       or_1_out, Q0, Q1, Q2, Q3, Q4, R, Z_out;
  wire [3:0] cnt_up_mod10_alargador_1_q;

  Clock clock_1 (.out(C));
  Button #(.press("passive")) Z (.out(Z_out));
  D_Flip_Flop FF0 (.D(FF0_qn), .clk(C), .Q(Q0), .Qn(FF0_qn), .reset(or_1_out));  // open: preset
  not not_1 (not_1_out, Z_out);
  or or_1 (or_1_out, not_1_out, R);
  J_K_Flip_Flop j_k_ff_1 (.J(1'b1), .K(1'b0), .clk(Q4), .Q(R), .reset(not_2_out));  // open: Qn, preset
  D_Flip_Flop FF1 (.D(FF1_qn), .clk(FF0_qn), .Q(Q1), .Qn(FF1_qn), .reset(or_1_out));  // open: preset
  not not_2 (not_2_out, C);
  D_Flip_Flop FF2 (.D(FF2_qn), .clk(FF1_qn), .Q(Q2), .Qn(FF2_qn), .reset(or_1_out));  // open: preset
  cnt_up_mod10_alargador cnt_up_mod10_alargador_1 (
    .clock(C), .z(Z_out), .q(cnt_up_mod10_alargador_1_q));  // open: clr_aux
  Hex_Digit_Display hex_digit_display_1 (.value(cnt_up_mod10_alargador_1_q));  // open: dp
  Hex_Digit_Display hex_digit_display_2 (.value({Q3, Q2, Q1, Q0}));  // open: dp
  D_Flip_Flop FF3 (.D(FF3_qn), .clk(FF2_qn), .Q(Q3), .Qn(FF3_qn), .reset(or_1_out));  // open: preset
  not not_3 (not_3_out, Q0);
  not not_4 (not_4_out, Q2);
  and and_1 (and_1_out, Q1, Q3);
  and and_2 (and_2_out, not_3_out, not_4_out);
  and and_3 (Q4, and_1_out, and_2_out);
endmodule

// VHDL entity comps, as the project stores it:
--------------------------------------------------------------------------------
-- UTFPR - Universidade Tecnológica Federal do Paraná - Curitiba - PR
-- Projeto  : Prática 5 - Cronômetro
-- Circuito : Implementação de um FF tipo D
-- Arquivo  : dff_vhdl.vhd
-- Autor    : prof. Gortan
-- Data     : Outubro 2021
--------------------------------------------------------------------------------
-- Descrição :
-- Implementa um flip-flop tipo D para ser usado como componente em outros circ.
-- obs.: para evitar que o Logisim-evolution 3.6.1 altere o nome do componente
--       introduzimos um componente "comps" no início do arquivo e o ff tipo d
--       vem em segundo lugar - No Quartus ele deve ser comentado / apagado
--------------------------------------------------------------------------------

--============================= Módulo comps: ==================================
library ieee;
  use ieee.std_logic_1164.all;

-- Comentar a entity comps e sua architecture quando usado no Quartus
-- Esse primeira entity é só um artifício para evitar que o Logisim
-- altere o nome do componente ff tipo d, que vem depois
entity comps is
  port(    a  : in  std_logic );
end comps;

architecture cmp_arch of comps is
-- Não faz nada:
begin
end cmp_arch;
-- Fim do trecho a comentar/apagar no Quartus

--==================== Componente: =============================================
library ieee;
  use ieee.std_logic_1164.all;

entity dff_vhdl is
  port(
    d, clk, prs, clr	: in  std_logic;	-- entradas: dado, clk, preset e clear
    q, qn				: out std_logic		-- saídas:   q e q invertido
 );
end dff_vhdl;

architecture ff_d of dff_vhdl is

	signal qstate: std_logic;

begin
	process(clk, clr, prs)
	begin
		if clr = '1' then qstate <= '0';
		elsif prs = '1' then qstate <= '1';
		elsif clk = '1' and clk' event then qstate <= d;
		end if;
	end process;
	q <= qstate;
	qn <= not qstate;
end ff_d;

// VHDL entity cnt_up_mod10_alargador, as the project stores it:
--------------------------------------------------------------------------------
-- Project :
-- File    :
-- Autor   :
-- Date    :
--
--------------------------------------------------------------------------------
-- Description :
--
--------------------------------------------------------------------------------

LIBRARY ieee;
USE ieee.std_logic_1164.all;

ENTITY cnt_up_mod10_alargador IS
  PORT (
  ------------------------------------------------------------------------------
  --Insert input ports below
   	clock, z      : IN  std_logic;                    -- input bit example
    	q        : INOUT  std_logic_vector(3 DOWNTO 0); -- input vector example
	clr_aux  : inout std_logic
    );
END cnt_up_mod10_alargador;

--------------------------------------------------------------------------------
--Complete your VHDL description below
--------------------------------------------------------------------------------

ARCHITECTURE TypeArchitecture OF cnt_up_mod10_alargador IS

component dff_vhdl is 
	port
	(
		d, clk, prs, clr	: in std_logic;
		q, qn			: out std_logic
	);
	end component;
	
	signal zn: std_logic;
	signal qn: std_logic_vector(3 downto 0);
	signal clear : std_logic;
	signal clkn: std_logic;

BEGIN
	zn <= not z;
	clear <= zn or (q(3) and q(1));
	ff_alargador: dff_vhdl port map(d => '0', clr => clkn, prs => clear, clk => '0', q => clr_aux, qn => open);
	ff_d0: dff_vhdl port map (d => qn(0), prs => '0', clr => clear, clk => clock, q => q(0), qn => qn(0));
	ff_d1: dff_vhdl port map (d => qn(1), prs => '0', clr => clear, clk => qn(0), q => q(1), qn => qn(1));
	ff_d2: dff_vhdl port map (d => qn(2), prs => '0', clr => clear, clk => qn(1), q => q(2), qn => qn(2));
	ff_d3: dff_vhdl port map (d => qn(3), prs => '0', clr => clear, clk => qn(2), q => q(3), qn => qn(3));

END TypeArchitecture;
