// Logisim project P5_funcionando.circ as structural Verilog
module P0_FFD (
);

  comps comps_1 ();  // open: a

  // Notes on the sheet:
  //   Este bloco de entidade VHDL contém duas entidades VHDL:
  //   A segunda chmada "ffd_vhdl", que será usada em todo este projeto:
  //   A primeira chamada "comps", que será renomeada e que não faz nada:
endmodule

module P1_cnt_mod16_up (
);

  wire clock_1_out, FF0_qn, FF1_qn, FF2_qn, FF3_qn, not_1_out, Q0, Q1, Q2, Q3, Z_out;
  wire [3:0] cnt_down_mod16_1_q;

  Clock clock_1 (.out(clock_1_out));
  Button #(.press("passive")) Z (.out(Z_out));
  D_Flip_Flop FF0 (.D(FF0_qn), .clk(clock_1_out), .Q(Q0), .Qn(FF0_qn), .preset(not_1_out));  // open: reset
  not not_1 (not_1_out, Z_out);
  D_Flip_Flop FF1 (.D(FF1_qn), .clk(Q0), .Q(Q1), .Qn(FF1_qn), .preset(not_1_out));  // open: reset
  D_Flip_Flop FF2 (.D(FF2_qn), .clk(Q1), .Q(Q2), .Qn(FF2_qn), .preset(not_1_out));  // open: reset
  cnt_down_mod16 cnt_down_mod16_1 (.clk(clock_1_out), .z(Z_out), .q(cnt_down_mod16_1_q));
  Hex_Digit_Display hex_digit_display_1 (.value(cnt_down_mod16_1_q));  // open: dp
  Hex_Digit_Display hex_digit_display_2 (.value({Q3, Q2, Q1, Q0}));  // open: dp
  D_Flip_Flop FF3 (.D(FF3_qn), .clk(Q2), .Q(Q3), .Qn(FF3_qn), .preset(not_1_out));  // open: reset
endmodule

// VHDL entity comps, as the project stores it:
--------------------------------------------------------------------------------
-- UTFPR - Universidade Tecnológica Federal do Paraná - Curitiba - PR
-- Projeto  : Prática 5 - Cronômetro
-- Circuito : Implementação de um FF tipo D
-- Arquivo  : dff_vhdl.vhd
-- Autor    : prof. Gortan
-- Data     : Outubro 2021
--------------------------------------------------------------------------------
-- Descrição :
-- Implementa um flip-flop tipo D para ser usado como componente em outros circ.
-- obs.: para evitar que o Logisim-evolution 3.6.1 altere o nome do componente
--       introduzimos um componente "comps" no início do arquivo e o ff tipo d
--       vem em segundo lugar - No Quartus ele deve ser comentado / apagado
--------------------------------------------------------------------------------

--============================= Módulo comps: ==================================
library ieee;
  use ieee.std_logic_1164.all;

-- Comentar a entity comps e sua architecture quando usado no Quartus
-- Esse primeira entity é só um artifício para evitar que o Logisim
-- altere o nome do componente ff tipo d, que vem depois
entity comps is
  port(    a  : in  std_logic );
end comps;

architecture cmp_arch of comps is
-- Não faz nada:
begin
end cmp_arch;
-- Fim do trecho a comentar/apagar no Quartus

--==================== Componente: =============================================
library ieee;
  use ieee.std_logic_1164.all;

entity dff_vhdl is
  port(
    d, clk, prs, clr	: in  std_logic;	-- entradas: dado, clk, preset e clear
    q, qn				: out std_logic		-- saídas:   q e q invertido
 );
end dff_vhdl;

architecture ff_d of dff_vhdl is

	signal qstate: std_logic;

begin
	process(clk, clr, prs)
	begin
		if clr = '1' then qstate <= '0';
		elsif prs = '1' then qstate <= '1';
		elsif clk = '1' and clk' event then qstate <= d;
		end if;
	end process;
	q <= qstate;
	qn <= not qstate;
end ff_d;

// VHDL entity cnt_down_mod16, as the project stores it:
--------------------------------------------------------------------------------
-- Project :
-- File    :
-- Autor   :
-- Date    :
--
--------------------------------------------------------------------------------
-- Description :
--
--------------------------------------------------------------------------------

LIBRARY ieee;
USE ieee.std_logic_1164.all;

ENTITY cnt_down_mod16 IS
  port(
    clk, z  : in  std_logic;					-- entradas clk, rst
    q       : inout std_logic_vector(3 downto 0)	-- saída q3 até q0
 );
END cnt_down_mod16;

--------------------------------------------------------------------------------
--Complete your VHDL description below
--------------------------------------------------------------------------------

ARCHITECTURE TypeArchitecture OF cnt_down_mod16 IS
	signal zn: std_logic;
	signal qn: std_logic_vector(3 downto 0);	-- liga qn com d
	component dff_vhdl is					-- dff referenciado como dff_vhdl
		port
		(
			d, clk, prs, clr	: in  std_logic;	-- entradas: dado, clk, preset e clear
			q, qn			: out std_logic 	-- saídas:   q e q invertido
		);
	end component;
begin
	zn <= not z;
	ff_d0: dff_vhdl port map(d => qn(0), prs => zn, clr => '0', clk => clk,  q => q(0), qn => qn(0));
	ff_d1: dff_vhdl port map(d => qn(1), prs => zn, clr => '0', clk => q(0), q => q(1), qn => qn(1));
	ff_d2: dff_vhdl port map(d => qn(2), prs => zn, clr => '0', clk => q(1), q => q(2), qn => qn(2));
	ff_d3: dff_vhdl port map(d => qn(3), prs => zn, clr => '0', clk => q(2), q => q(3), qn => qn(3));
	
END TypeArchitecture;
