// Logisim project P6.circ as structural Verilog
module P0_FFD (
);

  comps comps_1 ();  // open: a

  // Notes on the sheet:
  //   Este bloco de entidade VHDL contém duas entidades VHDL:
  //   A segunda chmada "ffd_vhdl", que será usada em todo este projeto:
  //   A primeira chamada "comps", que será renomeada e que não faz nada:
endmodule

module P1_cnt_mod16_up (
);

  wire clock_1_out, d_ff_1_q, F_out, FF0_qn, FF1_qn, FF2_qn, FF3_qn, not_1_out, or_1_out, Q0, Q1, Q2, Q3,
       RSTD, Z_out, ZR_out;
  wire [3:0] cnt_down_mod10_1_q;

  D_Flip_Flop FF0 (.D(FF0_qn), .clk(clock_1_out), .Q(Q0), .Qn(FF0_qn), .preset(or_1_out));  // open: reset
  Clock clock_1 (.out(clock_1_out));
  not not_1 (not_1_out, Z_out);
  Button #(.press("passive")) Z (.out(Z_out));
  D_Flip_Flop FF1 (.D(FF1_qn), .clk(Q0), .Q(Q1), .Qn(FF1_qn), .reset(or_1_out));  // open: preset
  and F (F_out, Q0, Q1, Q2, Q3);
  nor ZR (ZR_out, Q0, Q1, Q2, Q3);
  D_Flip_Flop d_ff_1 (.Q(d_ff_1_q), .preset(ZR_out), .reset(RSTD));  // open: D, clk, Qn
  D_Flip_Flop FF2 (.D(FF2_qn), .clk(Q1), .Q(Q2), .Qn(FF2_qn), .reset(or_1_out));  // open: preset
  cnt_down_mod10 cnt_down_mod10_1 (.clk(clock_1_out), .z(Z_out), .q(cnt_down_mod10_1_q));
  Hex_Digit_Display hex_digit_display_1 (.value(cnt_down_mod10_1_q));  // open: dp
  and R (RSTD, F_out, d_ff_1_q);
  D_Flip_Flop FF3 (.D(FF3_qn), .clk(Q2), .Q(Q3), .Qn(FF3_qn), .preset(or_1_out));  // open: reset
  or or_1 (or_1_out, not_1_out, RSTD);
  Hex_Digit_Display hex_digit_display_2 (.value({Q3, Q2, Q1, Q0}));  // open: dp
endmodule

// VHDL entity comps, as the project stores it:
--------------------------------------------------------------------------------
-- UTFPR - Universidade Tecnológica Federal do Paraná - Curitiba - PR
-- Projeto  : Prática 5 - Cronômetro
-- Circuito : Implementação de um FF tipo D
-- Arquivo  : dff_vhdl.vhd
-- Autor    : prof. Gortan
-- Data     : Outubro 2021
--------------------------------------------------------------------------------
-- Descrição :
-- Implementa um flip-flop tipo D para ser usado como componente em outros circ.
-- obs.: para evitar que o Logisim-evolution 3.6.1 altere o nome do componente
--       introduzimos um componente "comps" no início do arquivo e o ff tipo d
--       vem em segundo lugar - No Quartus ele deve ser comentado / apagado
--------------------------------------------------------------------------------

--============================= Módulo comps: ==================================
library ieee;
  use ieee.std_logic_1164.all;

-- Comentar a entity comps e sua architecture quando usado no Quartus
-- Esse primeira entity é só um artifício para evitar que o Logisim
-- altere o nome do componente ff tipo d, que vem depois
entity comps is
  port(    a  : in  std_logic );
end comps;

architecture cmp_arch of comps is
-- Não faz nada:
begin
end cmp_arch;
-- Fim do trecho a comentar/apagar no Quartus

--==================== Componente: =============================================
library ieee;
  use ieee.std_logic_1164.all;

entity dff_vhdl is
  port(
    d, clk, prs, clr	: in  std_logic;	-- entradas: dado, clk, preset e clear
    q, qn				: out std_logic		-- saídas:   q e q invertido
 );
end dff_vhdl;

architecture ff_d of dff_vhdl is

	signal qstate: std_logic;

begin
	process(clk, clr, prs)
	begin
		if clr = '1' then qstate <= '0';
		elsif prs = '1' then qstate <= '1';
		elsif clk = '1' and clk' event then qstate <= d;
		end if;
	end process;
	q <= qstate;
	qn <= not qstate;
end ff_d;

// VHDL entity cnt_down_mod10, as the project stores it:
-------------------- ------------------------------------------------------------
-- UTFPR - Universidade Tecnológica Federal do Paraná - Curitiba - PR
-- Projeto  : Prática 5 - Cronômetro
-- Circuito : Contador assíncrono ascendente módulo 16
-- Arquivo  : cnt_up_mod16_vhdl.vhd
-- Autor    : prof. Gortan
-- Data     : Outubro 2021
--------------------------------------------------------------------------------
-- Descrição :
-- Implementa um contador assíncrono ascendente módulo 16
-- Utiliza ffs tipo D com resposta a flanco positivo do clock e clear e preset
-- assíncronos ativos em alto (componente dff_vhdl)
--------------------------------------------------------------------------------

--============================= Nível Superior: =========================================
--------------------------------------------------------------------------------
-- Project :
-- File    :
-- Autor   :
-- Date    :
--
--------------------------------------------------------------------------------
-- Description :
--
--------------------------------------------------------------------------------

LIBRARY ieee;
USE ieee.std_logic_1164.all;

ENTITY cnt_down_mod10 IS
  port(
    clk, z  : in  std_logic;					-- entradas clk, rst
    q       : inout std_logic_vector(3 downto 0)	-- saída q3 até q0
 );
END cnt_down_mod10;

--------------------------------------------------------------------------------
--Complete your VHDL description below
--------------------------------------------------------------------------------

ARCHITECTURE TypeArchitecture OF cnt_down_mod10 IS
	signal zn: std_logic;
	signal qn: std_logic_vector(3 downto 0);	-- liga qn com d
	component dff_vhdl is					-- dff referenciado como dff_vhdl
		port
		(
			d, clk, prs, clr	: in  std_logic;	-- entradas: dado, clk, preset e clear
			q, qn			: out std_logic 	-- saídas:   q e q invertido
		);
	end component;
	signal clear: std_logic;
	signal aux1: std_logic;
	signal aux2: std_logic;
	signal r: std_logic;
begin
	zn <= not z;
	
	aux1 <= q(0) and q(1) and q(2) and q(3);
	aux2 <= (((q(0) nor q(1)) nor q(2)) nor q(3));
	
	clear <= zn nand (r nand aux1);
	
	ff_d0: dff_vhdl port map(d => qn(0), prs => clear, clr => '0', clk => clk,  q => q(0), qn => qn(0));
	ff_d1: dff_vhdl port map(d => qn(1), prs => '0', clr => clear, clk => q(0), q => q(1), qn => qn(1));
	ff_d2: dff_vhdl port map(d => qn(2), prs => '0', clr => clear, clk => q(1), q => q(2), qn => qn(2));
	ff_d3: dff_vhdl port map(d => qn(3), prs => clear, clr => '0', clk => q(2), q => q(3), qn => qn(3));
	ff_reset: dff_vhdl port map(d => '0', prs => aux2, clr => clear, clk => '0', q => r, qn => open); 

END TypeArchitecture;
