// Logisim project P7_2.circ as structural Verilog
module P0_FFD (
);

  comps comps_1 ();  // open: a

  // Notes on the sheet:
  //   Este bloco de entidade VHDL contém duas entidades VHDL:
  //   A segunda chmada "ffd_vhdl", que será usada em todo este projeto:
  //   A primeira chamada "comps", que será renomeada e que não faz nada:
endmodule

module P1_cnt_mod16_up (
);

  wire C, clock_1_out, d_ff_1_q, F_out, FF0_qn, FF1_qn, FF2_qn, FF3_qn, not_2_out, or_1_out, Q0, Q1, Q2, Q3,
       R_out, RSTD, Z_out, ZR_out;
  wire [3:0] cnt_down_mod10_alargador_vhdl_1_q;

  Clock clock_1 (.out(clock_1_out));
  D_Flip_Flop FF0 (.D(FF0_qn), .clk(clock_1_out), .Q(Q0), .Qn(FF0_qn), .preset(or_1_out));  // open: reset
  not not_1 (C, clock_1_out);
  D_Flip_Flop FF1 (.D(FF1_qn), .clk(Q0), .Q(Q1), .Qn(FF1_qn), .reset(or_1_out));  // open: preset
  and F (F_out, Q0, Q1, Q2, Q3);
  D_Flip_Flop FF2 (.D(FF2_qn), .clk(Q1), .Q(Q2), .Qn(FF2_qn), .reset(or_1_out));  // open: preset
  nor ZR (ZR_out, Q0, Q1, Q2, Q3);
  D_Flip_Flop d_ff_1 (.Q(d_ff_1_q), .preset(ZR_out), .reset(RSTD));  // open: D, clk, Qn
  and R (R_out, F_out, d_ff_1_q);
  D_Flip_Flop FF3 (.D(FF3_qn), .clk(Q2), .Q(Q3), .Qn(FF3_qn), .preset(or_1_out));  // open: reset
  or or_1 (or_1_out, not_2_out, RSTD);
  not not_2 (not_2_out, Z_out);
  Button #(.press("passive")) Z (.out(Z_out));
  cnt_down_mod10_alargador_vhdl cnt_down_mod10_alargador_vhdl_1 (
    .clk(clock_1_out), .z(not_2_out), .q(cnt_down_mod10_alargador_vhdl_1_q));
  D_Flip_Flop d_ff_2 (.Q(RSTD), .preset(R_out), .reset(C));  // open: D, clk, Qn
  Hex_Digit_Display hex_digit_display_1 (.value({Q3, Q2, Q1, Q0}));  // open: dp
  Hex_Digit_Display hex_digit_display_2 (.value(cnt_down_mod10_alargador_vhdl_1_q));  // open: dp
endmodule

// VHDL entity comps, as the project stores it:
--------------------------------------------------------------------------------
-- UTFPR - Universidade Tecnológica Federal do Paraná - Curitiba - PR
-- Projeto  : Prática 5 - Cronômetro
-- Circuito : Implementação de um FF tipo D
-- Arquivo  : dff_vhdl.vhd
-- Autor    : prof. Gortan
-- Data     : Outubro 2021
--------------------------------------------------------------------------------
-- Descrição :
-- Implementa um flip-flop tipo D para ser usado como componente em outros circ.
-- obs.: para evitar que o Logisim-evolution 3.6.1 altere o nome do componente
--       introduzimos um componente "comps" no início do arquivo e o ff tipo d
--       vem em segundo lugar - No Quartus ele deve ser comentado / apagado
--------------------------------------------------------------------------------

--============================= Módulo comps: ==================================
library ieee;
  use ieee.std_logic_1164.all;

-- Comentar a entity comps e sua architecture quando usado no Quartus
-- Esse primeira entity é só um artifício para evitar que o Logisim
-- altere o nome do componente ff tipo d, que vem depois
entity comps is
  port(    a  : in  std_logic );
end comps;

architecture cmp_arch of comps is
-- Não faz nada:
begin
end cmp_arch;
-- Fim do trecho a comentar/apagar no Quartus

--==================== Componente: =============================================
library ieee;
  use ieee.std_logic_1164.all;

entity dff_vhdl is
  port(
    d, clk, prs, clr	: in  std_logic;	-- entradas: dado, clk, preset e clear
    q, qn				: out std_logic		-- saídas:   q e q invertido
 );
end dff_vhdl;

architecture ff_d of dff_vhdl is

	signal qstate: std_logic;

begin
	process(clk, clr, prs)
	begin
		if clr = '1' then qstate <= '0';
		elsif prs = '1' then qstate <= '1';
		elsif clk = '1' and clk' event then qstate <= d;
		end if;
	end process;
	q <= qstate;
	qn <= not qstate;
end ff_d;

// VHDL entity cnt_down_mod10_alargador_vhdl, as the project stores it:
library ieee;
use ieee.std_logic_1164.all;

entity cnt_down_mod10_alargador_vhdl is
  port(
    clk, z  : in  std_logic;					
    q       : out std_logic_vector(3 downto 0)	
 );
end cnt_down_mod10_alargador_vhdl;

architecture cnt_down_mod10_alargador_arch of cnt_down_mod10_alargador_vhdl is
	signal zn: std_logic;
	signal qn: std_logic_vector(3 downto 0);	
	signal qstate: std_logic_vector(3 downto 0);
	signal rst, ff_rst_in, ff_rst_out, clkn, prs_rst, ff_rst, clr_alargador, clr_aux: std_logic;
	component dff_vhdl is					
		port
		(
			d, clk, prs, clr	: in  std_logic;
			q, qn			: out std_logic
		);
	end component;
begin
	zn <= not z;
	clkn <= not clk;
	rst <= ff_rst_out and (qstate(0) and (qstate(1) and (qstate(2) and qstate(3))));
	ff_rst_in <= not (qstate(0) or (qstate(1) or (qstate(2) or qstate(3))));
	prs_rst <= rst or zn;
	ff_d0:                  dff_vhdl port map(d => qn(0), prs => clr_aux,   clr => '0',    clk => clk,       q => qstate(0), qn => qn(0));
	ff_d1:                  dff_vhdl port map(d => qn(1), prs => '0',       clr => ff_rst, clk => qstate(0), q => qstate(1), qn => qn(1));
	ff_d2:                  dff_vhdl port map(d => qn(2), prs => '0',       clr => ff_rst, clk => qstate(1), q => qstate(2), qn => qn(2));
	ff_d3:                  dff_vhdl port map(d => qn(3), prs => clr_aux,   clr => '0',    clk => qstate(2), q => qstate(3), qn => qn(3));
	ff_reset:               dff_vhdl port map(d => '0',   prs => ff_rst_in, clr => ff_rst, clk => '0',       q => ff_rst_out);
	ff_reset_alargador:     dff_vhdl port map(d => '0',   prs => prs_rst,   clr => clkn,   clk => '0',       q => ff_rst);
	ff_reset_clr_alargador: dff_vhdl port map(d => '0',   prs => zn,        clr => clkn,   clk => '0',       q => clr_alargador);
	clr_aux <= clr_alargador;
	q(0) <= qstate(0);
	q(1) <= qstate(1);
	q(2) <= qstate(2);
	q(3) <= qstate(3);
end cnt_down_mod10_alargador_arch;
