// Logisim project ex1.circ as structural Verilog
module ex1 (
  input  SST,
  input  UD,
  input  Z
);

  wire CLK_out;
  wire [6:0] cronometro_sincrono_1_display_dezena, cronometro_sincrono_1_display_unidade;

  Clock CLK (.out(CLK_out));
  cronometro_sincrono cronometro_sincrono_1 (
    .clk(CLK_out), .start_stop(SST), .ud(UD), .Z(Z), .display_unidade(cronometro_sincrono_1_display_unidade),
    .display_dezena(cronometro_sincrono_1_display_dezena));
  _7_Segment_Display u_7_segment_display_1 (
    .g(cronometro_sincrono_1_display_unidade[0]), .f(cronometro_sincrono_1_display_unidade[1]),
    .a(cronometro_sincrono_1_display_unidade[6]), .b(cronometro_sincrono_1_display_unidade[5]),
    .e(cronometro_sincrono_1_display_unidade[2]), .d(cronometro_sincrono_1_display_unidade[3]),
    .c(cronometro_sincrono_1_display_unidade[4]));  // open: dp
  _7_Segment_Display u_7_segment_display_2 (
    .g(cronometro_sincrono_1_display_dezena[0]), .f(cronometro_sincrono_1_display_dezena[1]),
    .a(cronometro_sincrono_1_display_dezena[6]), .b(cronometro_sincrono_1_display_dezena[5]),
    .e(cronometro_sincrono_1_display_dezena[2]), .d(cronometro_sincrono_1_display_dezena[3]),
    .c(cronometro_sincrono_1_display_dezena[4]));  // open: dp
endmodule

module ex2 (
);

  wire CLK_out, start_out;
  wire [6:0] undriven, undriven_2;

  Clock CLK (.out(CLK_out));
  Button start (.out(start_out));
  _7_Segment_Display u_7_segment_display_1 (
    .g(undriven_2[0]), .f(undriven_2[1]), .a(undriven_2[6]), .b(undriven_2[5]), .e(undriven_2[2]),
    .d(undriven_2[3]), .c(undriven_2[4]));  // open: dp
  _7_Segment_Display u_7_segment_display_2 (
    .g(undriven[0]), .f(undriven[1]), .a(undriven[6]), .b(undriven[5]), .e(undriven[2]), .d(undriven[3]),
    .c(undriven[4]));  // open: dp
endmodule

// VHDL entity cnt_up_down_mod10_vhdl, as the project stores it:
library ieee;
use ieee.std_logic_1164.all;
	
entity cnt_up_down_mod10_vhdl is
	port(
		clk, z, ud	: in  std_logic;					
	    	q       		: out std_logic_vector(3 downto 0);	
	    	co 			: out std_logic
	 );
end cnt_up_down_mod10_vhdl;
	
architecture nt_up_down_mod10_arch of cnt_up_down_mod10_vhdl is
	signal q_up, q_down, qstate_up, qstate_down, qn_up, qn_down: std_logic_vector(3 downto 0);
	signal clk_up, clk_down, clkn_up, clkn_down, rst, zn, reset, ff_rst_in, ff_rst_out, rst_alargador, ff_rst, clr_alargador, clr_aux, prs_rst: std_logic;	
	component dff_vhdl is					-- dff referenciado como dff_vhdl
		port(
			d, clk, prs, clr	: in  std_logic;	-- entradas: dado, clk, preset e clear
			q, qn			: out std_logic 	-- saídas:   q e q invertido
		);
	end component;
begin
	q(0) <= q_up(0) when ud = '0' else q_down(0);
	q(1) <= q_up(1) when ud = '0' else q_down(1);
	q(2) <= q_up(2) when ud = '0' else q_down(2);
	q(3) <= q_up(3) when ud = '0' else q_down(3);
	zn <= not z;
	clk_up <= clk when ud = '0';
	clk_down <= clk when ud = '1';
	clkn_up <= not clk_up;
	clkn_down <= not clk_down;
	prs_rst <= (zn or (qstate_up(1) and qstate_up(3)));
	ff_d0_up: dff_vhdl port map(d => qn_up(0), prs => '0', clr => clr_aux, clk => clk_up,   q => qstate_up(0), qn => qn_up(0));
	ff_d1_up: dff_vhdl port map(d => qn_up(1), prs => '0', clr => clr_aux, clk => qn_up(0), q => qstate_up(1), qn => qn_up(1));
	ff_d2_up: dff_vhdl port map(d => qn_up(2), prs => '0', clr => clr_aux, clk => qn_up(1), q => qstate_up(2), qn => qn_up(2));
	ff_d3_up: dff_vhdl port map(d => qn_up(3), prs => '0', clr => clr_aux, clk => qn_up(2), q => qstate_up(3), qn => qn_up(3));
	ff_rst_up: dff_vhdl port map(d => '0', prs => prs_rst, clr => clkn_up, clk => '0', q => clr_aux);
	q_up(0) <= qstate_up(0);
	q_up(1) <= qstate_up(1);
	q_up(2) <= qstate_up(2);
	q_up(3) <= qstate_up(3);
	reset <= ff_rst_out and (qstate_down(0) and (qstate_down(1) and (qstate_down(2) and qstate_down(3))));
	ff_rst_in <= not (qstate_down(0) or (qstate_down(1) or (qstate_down(2) or qstate_down(3))));
	rst_alargador <= reset or zn;
	ff_d0_down: dff_vhdl port map(d => qn_down(0), prs => rst, clr => '0', clk => clk_down, q => qstate_down(0), qn => qn_down(0));
	ff_d1_down: dff_vhdl port map(d => qn_down(1), prs => '0', clr => ff_rst, clk => qstate_down(0), q => qstate_down(1), qn => qn_down(1));
	ff_d2_down: dff_vhdl port map(d => qn_down(2), prs => '0', clr => ff_rst, clk => qstate_down(1), q => qstate_down(2), qn => qn_down(2));
	ff_d3_down: dff_vhdl port map(d => qn_down(3), prs => rst, clr => '0', clk => qstate_down(2), q => qstate_down(3), qn => qn_down(3));
	ff_rst_down: dff_vhdl port map(d => '0', prs => ff_rst_in, clr => ff_rst, clk => '0', q => ff_rst_out);
	ff_rst_alargador_down: dff_vhdl   port map(d => '0', prs => rst_alargador, clr => clkn_down, clk => '0', q => ff_rst);
	ff_rst_alargador_clr_down: dff_vhdl port map(d => '0', prs => zn, clr => clkn_down, clk => '0', q => clr_alargador);
	rst <= '1' when clr_alargador = '1' else '0';
	q_down(0) <= qstate_down(0);
	q_down(1) <= qstate_down(1);
	q_down(2) <= qstate_down(2);
	q_down(3) <= qstate_down(3);
	co <= clr_aux when ud = '0' else ff_rst;
end nt_up_down_mod10_arch;

// VHDL entity cronometro_sincrono, as the project stores it:
library ieee;
use ieee.std_logic_1164.all;
use ieee.std_logic_unsigned.all;


entity cronometro_sincrono is
    port (
        clk         : in  std_logic; 
        start_stop  : in  std_logic; 
        ud          : in  std_logic; 
        Z           : in  std_logic; 
        display_unidade : out std_logic_vector(6 downto 0); 
        display_dezena  : out std_logic_vector(6 downto 0)  
    );
end entity cronometro_sincrono;

architecture Arch_cronometro of cronometro_sincrono is

    function decode_7s(signal count: std_logic_vector) return std_logic_vector is
        variable v_in: std_logic_vector(3 downto 0) := count;
        variable result: std_logic_vector(6 downto 0) := "1111111";
    begin
        case v_in is
            when "0000" => result := "1111110";  -- 0
            when "0001" => result := "0110000";  -- 1
            when "0010" => result := "1101101";  -- 2
            when "0011" => result := "1111001";  -- 3
            when "0100" => result := "0110011";  -- 4
            when "0101" => result := "1011011";  -- 5
            when "0110" => result := "1011111";  -- 6 
            when "0111" => result := "1110000";  -- 7
            when "1000" => result := "1111111";  -- 8
            when "1001" => result := "1111011";  -- 9
            when others => result := "0000000";  -- Apagado
        end case;
        return result;
    end function decode_7s;

    -- Sinais internos para os contadores (00-59)
    signal unidade : std_logic_vector(3 downto 0) := "0000";
    signal dezena  : std_logic_vector(3 downto 0) := "0000"; -- Usa 4 bits, mas a lógica só conta 0-5

    -- Sinais internos para a lógica de controle
    signal running   : std_logic := '0'; -- '1' = contando, '0' = pausado
    signal direction : std_logic := '0'; -- '0' = up, '1' = down
    
    -- Sinal para detectar a borda do botão start_stop (para o toggle)
    signal start_stop_last : std_logic := '0';

begin

    -- Processo principal do cronômetro
    -- Sensível ao clock (para contagem) e ao Z (reset assíncrono)
    main_process: process(clk, Z)
    begin
        if Z = '1' then
            -- Reset e suspensão 
            unidade   <= "0000";
            dezena    <= "0000";
            running   <= '0'; -- Para a contagem 
            -- A mudança de sentido SÓ ocorre com Z acionado [cite: 36]
            direction <= ud; 
            start_stop_last <= '0'; -- Reseta o detector de borda

        elsif rising_edge(clk) then
            
            -- Lógica do botão Start/Stop (detecta borda de subida)
            -- Isso faz o botão funcionar como um "toggle" (liga/desliga)
            if start_stop = '1' and start_stop_last = '0' then
                running <= not running; -- Inverte o estado (pausa/continua) 
            end if;
            start_stop_last <= start_stop; -- Armazena o estado anterior do botão

            -- Lógica de contagem (só conta se running = '1')
            if running = '1' then
                if direction = '0' then -- Contagem Ascendente ('0' = low) 
                    if unidade = "1001" then -- se unidade = 9
                        unidade <= "0000";
                        if dezena = "0101" then -- se dezena = 5 (chegou em 59)
                            dezena <= "0000"; -- Rola de 59 para 00
                        else
                            dezena <= dezena + 1;
                        end if;
                    else
                        unidade <= unidade + 1;
                    end if;
                else -- Contagem Descendente ('1' = high) 
                    if unidade = "0000" then -- se unidade = 0
                        unidade <= "1001";
                        if dezena = "0000" then -- se dezena = 0 (chegou em 00)
                            dezena <= "0101"; -- Rola de 00 para 59
                        else
                            dezena <= dezena - 1;
                        end if;
                    else
                        unidade <= unidade - 1;
                    end if;
                end if;
            end if; -- end if running
        end if; -- end if rising_edge
    end process main_process;

    -- Lógica de saída: conecta os contadores aos displays
    display_unidade <= decode_7s(unidade);
    display_dezena  <= decode_7s(dezena);

end architecture Arch_cronometro;
