// Logisim project lab06.circ as structural Verilog
module ex1 (
  input  Z,
  input  UD,
  input  SST
);

  wire CLK_out;
  wire [6:0] p1_cronometro_sincrono_vhdl_1_qd_7s, p1_cronometro_sincrono_vhdl_1_qu_7s;

  Clock CLK (.out(CLK_out));
  P1_cronometro_sincrono_vhdl p1_cronometro_sincrono_vhdl_1 (
    .clk(CLK_out), .z(Z), .ud(UD), .sst(SST), .qu_7s(p1_cronometro_sincrono_vhdl_1_qu_7s),
    .qd_7s(p1_cronometro_sincrono_vhdl_1_qd_7s));
  _7_Segment_Display u_7_segment_display_1 (
    .g(p1_cronometro_sincrono_vhdl_1_qu_7s[0]), .f(p1_cronometro_sincrono_vhdl_1_qu_7s[1]),
    .a(p1_cronometro_sincrono_vhdl_1_qu_7s[6]), .b(p1_cronometro_sincrono_vhdl_1_qu_7s[5]),
    .e(p1_cronometro_sincrono_vhdl_1_qu_7s[2]), .d(p1_cronometro_sincrono_vhdl_1_qu_7s[3]),
    .c(p1_cronometro_sincrono_vhdl_1_qu_7s[4]));  // open: dp
  _7_Segment_Display u_7_segment_display_2 (
    .g(p1_cronometro_sincrono_vhdl_1_qd_7s[0]), .f(p1_cronometro_sincrono_vhdl_1_qd_7s[1]),
    .a(p1_cronometro_sincrono_vhdl_1_qd_7s[6]), .b(p1_cronometro_sincrono_vhdl_1_qd_7s[5]),
    .e(p1_cronometro_sincrono_vhdl_1_qd_7s[2]), .d(p1_cronometro_sincrono_vhdl_1_qd_7s[3]),
    .c(p1_cronometro_sincrono_vhdl_1_qd_7s[4]));  // open: dp
endmodule

// VHDL entity cnt_up_down_mod10_vhdl, as the project stores it:
library ieee;
use ieee.std_logic_1164.all;
	
entity cnt_up_down_mod10_vhdl is
	port(
		clk, z, ud	: in  std_logic;					
	    	q       		: out std_logic_vector(3 downto 0);	
	    	co 			: out std_logic
	 );
end cnt_up_down_mod10_vhdl;
	
architecture nt_up_down_mod10_arch of cnt_up_down_mod10_vhdl is
	signal q_up, q_down, qstate_up, qstate_down, qn_up, qn_down: std_logic_vector(3 downto 0);
	signal clk_up, clk_down, clkn_up, clkn_down, rst, zn, reset, ff_rst_in, ff_rst_out, rst_alargador, ff_rst, clr_alargador, clr_aux, prs_rst: std_logic;	
	component dff_vhdl is					-- dff referenciado como dff_vhdl
		port(
			d, clk, prs, clr	: in  std_logic;	-- entradas: dado, clk, preset e clear
			q, qn			: out std_logic 	-- saídas:   q e q invertido
		);
	end component;
begin
	q(0) <= q_up(0) when ud = '0' else q_down(0);
	q(1) <= q_up(1) when ud = '0' else q_down(1);
	q(2) <= q_up(2) when ud = '0' else q_down(2);
	q(3) <= q_up(3) when ud = '0' else q_down(3);
	zn <= not z;
	clk_up <= clk when ud = '0';
	clk_down <= clk when ud = '1';
	clkn_up <= not clk_up;
	clkn_down <= not clk_down;
	prs_rst <= (zn or (qstate_up(1) and qstate_up(3)));
	ff_d0_up: dff_vhdl port map(d => qn_up(0), prs => '0', clr => clr_aux, clk => clk_up,   q => qstate_up(0), qn => qn_up(0));
	ff_d1_up: dff_vhdl port map(d => qn_up(1), prs => '0', clr => clr_aux, clk => qn_up(0), q => qstate_up(1), qn => qn_up(1));
	ff_d2_up: dff_vhdl port map(d => qn_up(2), prs => '0', clr => clr_aux, clk => qn_up(1), q => qstate_up(2), qn => qn_up(2));
	ff_d3_up: dff_vhdl port map(d => qn_up(3), prs => '0', clr => clr_aux, clk => qn_up(2), q => qstate_up(3), qn => qn_up(3));
	ff_rst_up: dff_vhdl port map(d => '0', prs => prs_rst, clr => clkn_up, clk => '0', q => clr_aux);
	q_up(0) <= qstate_up(0);
	q_up(1) <= qstate_up(1);
	q_up(2) <= qstate_up(2);
	q_up(3) <= qstate_up(3);
	reset <= ff_rst_out and (qstate_down(0) and (qstate_down(1) and (qstate_down(2) and qstate_down(3))));
	ff_rst_in <= not (qstate_down(0) or (qstate_down(1) or (qstate_down(2) or qstate_down(3))));
	rst_alargador <= reset or zn;
	ff_d0_down: dff_vhdl port map(d => qn_down(0), prs => rst, clr => '0', clk => clk_down, q => qstate_down(0), qn => qn_down(0));
	ff_d1_down: dff_vhdl port map(d => qn_down(1), prs => '0', clr => ff_rst, clk => qstate_down(0), q => qstate_down(1), qn => qn_down(1));
	ff_d2_down: dff_vhdl port map(d => qn_down(2), prs => '0', clr => ff_rst, clk => qstate_down(1), q => qstate_down(2), qn => qn_down(2));
	ff_d3_down: dff_vhdl port map(d => qn_down(3), prs => rst, clr => '0', clk => qstate_down(2), q => qstate_down(3), qn => qn_down(3));
	ff_rst_down: dff_vhdl port map(d => '0', prs => ff_rst_in, clr => ff_rst, clk => '0', q => ff_rst_out);
	ff_rst_alargador_down: dff_vhdl   port map(d => '0', prs => rst_alargador, clr => clkn_down, clk => '0', q => ff_rst);
	ff_rst_alargador_clr_down: dff_vhdl port map(d => '0', prs => zn, clr => clkn_down, clk => '0', q => clr_alargador);
	rst <= '1' when clr_alargador = '1' else '0';
	q_down(0) <= qstate_down(0);
	q_down(1) <= qstate_down(1);
	q_down(2) <= qstate_down(2);
	q_down(3) <= qstate_down(3);
	co <= clr_aux when ud = '0' else ff_rst;
end nt_up_down_mod10_arch;

// VHDL entity cnt_up_down_mod60_vhdl, as the project stores it:
library ieee;
use ieee.std_logic_1164.all;
use ieee.std_logic_unsigned.all;

-- A entidade é baseada no nome da arquitetura da imagem [cite: 42]
entity Sequencia is
    port (
        -- Entradas baseadas no processo da imagem [cite: 77]
        clock, start : in  std_logic; 
        -- Saída baseada na atribuição final da imagem [cite: 90]
        valor        : out std_logic_vector(6 downto 0) 
    );
end entity Sequencia;

architecture arch of Sequencia is
    -- Sinal interno para o contador, como na imagem [cite: 77]
    signal slsd: std_logic_vector(3 downto 0) := "0000";
begin

    -- Processo de contagem, lógica idêntica à da imagem 
    count: process(clock, start)
        variable vlsd: std_logic_vector(3 downto 0) := "0000"; [cite: 78]
    begin
        -- Reset [cite: 79]
        if rising_edge(start) then
            vlsd := "0000";
        end if;

        -- Lógica de contagem [cite: 81]
        if(rising_edge(clock)) then
            vlsd := vlsd + 1; [cite: 82]
            -- Rollover de 9 para 0 (quando vlsd = 1010) [cite: 83, 85]
            if(vlsd = "1010") then
                vlsd := "0000"; -- Corrigido de 'vlsd:="0000"' 
            end if;
        end if;

        -- Atribui a variável ao sinal [cite: 88]
        slsd <= vlsd;
    end process count;

    -- Decodificador BCD para 7 segmentos
    -- Estilo "with select" do seu exemplo, aplicado ao sinal 'slsd'
    -- Os valores são do seu exemplo e da imagem [cite: 50, 56, 62, 68]
    with slsd select
        valor <= "1111110" when "0000", -- 0 [cite: 50]
                 "0110000" when "0001", -- 1 [cite: 56]
                 "1101101" when "0010", -- 2 (do seu exemplo)
                 "1111001" when "0011", -- 3 (do seu exemplo)
                 "0110011" when "0100", -- 4 (do seu exemplo)
                 "1011011" when "0101", -- 5 (do seu exemplo)
                 "1011111" when "0110", -- 6 (do seu exemplo)
                 "1110000" when "0111", -- 7 (do seu exemplo)
                 "1111111" when "1000", -- 8 [cite: 62]
                 "1111011" when "1001", -- 9 [cite: 68]
                 "0000000" when others; -- Default para valores > 9
end architecture arch;

// VHDL entity P1_cronometro_sincrono_vhdl, as the project stores it:
library ieee;
use ieee.std_logic_1164.all;
use ieee.std_logic_unsigned.all;

entity P1_cronometro_sincrono_vhdl is
	port (
		clk, z, ud, sst	:	in std_logic; 
		qu_7s, qd_7s		:	out std_logic_vector(6 downto 0)
	);
end P1_cronometro_sincrono_vhdl;

architecture cronometro_sincrono_arch of P1_cronometro_sincrono_vhdl is
	signal u, qu: std_logic_vector(3 downto 0);
	signal d, qd: std_logic_vector(2 downto 0);
begin
    proc: process(clk, z)
    begin
        if z = '1' then
            if ud = '1' then
                u <= "0000";
                d <= "000";
            else
                u <= "1001";
                d <= "101";
            end if;
        elsif sst = '1' then
            if clk = '1'  and clk' event then
                if ud = '1' then
                    if u < "1001" then
                        u <= u + "0001";
                    else
                        u <= "0000";
                        if d < "101" then
                            d <= d + "001";
                        else 
                            d <= "000";
                        end if;
                    end if;
                else
                    if u > "0000" then
                        u <= u - "0001";
                    else
                        u <= "1001";
                        if d > "000" then
                            d <= d - "001";
                        else 
                            d <= "101";
                        end if;
                    end if;
                end if;
            end if;
        end if;
   	end process proc;
	qu(0) <= u(0);
	qu(1) <= u(1);
	qu(2) <= u(2);
	qu(3) <= u(3);
	qd(0) <= d(0);
	qd(1) <= d(1);
	qd(2) <= d(2);
	with qu select
		qu_7s <=	"1111110" when "0000",
				"0110000" when "0001",
				"1101101" when "0010",
				"1111001" when "0011",
				"0110011" when "0100",
				"1011011" when "0101",
				"1011111" when "0110",
				"1110000" when "0111",
				"1111111" when "1000",
				"1110011" when "1001",
				"1110111" when "1010",
				"0011111" when "1011",
				"1001110" when "1100",
				"0111101" when "1101",
				"1111001" when "1110",
				"0111100" when "1111",
				"0000000" when others;
	with qd select
     	qd_7s <=	"1111110" when "000",
				"0110000" when "001",
				"1101101" when "010",
				"1111001" when "011",
				"0110011" when "100",
				"1011011" when "101",
				"1011111" when "110",
				"1110000" when "111",
				"0000000" when others;
end cronometro_sincrono_arch;
