// Logisim project det_111.circ as structural Verilog
module sld_03 (
  input  S
);

  wire and_1_out, and_2_out, and_3_out, and_4_out, and_5_out, and_6_out, and_7_out, and_8_out, button_1_out,
       clock_1_out, det_seq_111_1_det_out, or_1_out, or_2_out, or_3_out;
  wire [2:0] FF0_q;
  wire [3:0] det_seq_111_1_est_out;

  Button button_1 (.out(button_1_out));
  Clock clock_1 (.out(clock_1_out));
  D_Flip_Flop FF0 (.D(or_3_out), .clk(clock_1_out), .Q(FF0_q[0]), .reset(button_1_out));  // open: Qn, preset
  D_Flip_Flop FF1 (.D(or_2_out), .clk(clock_1_out), .Q(FF0_q[1]), .reset(button_1_out));  // open: Qn, preset
  D_Flip_Flop FF2 (.D(or_1_out), .clk(clock_1_out), .Q(FF0_q[2]), .reset(button_1_out));  // open: Qn, preset
  Hex_Digit_Display hex_digit_display_1 (.value({1'b0, FF0_q}));  // open: dp
  and and_1 (and_1_out, FF0_q[2], ~FF0_q[1], ~FF0_q[0], ~S);  // AND_Gate
  and and_2 (and_2_out, ~FF0_q[2], FF0_q[1], FF0_q[0], S);  // AND_Gate
  and and_3 (and_3_out, ~FF0_q[1], FF0_q[0], S);  // AND_Gate
  and and_4 (and_4_out, ~FF0_q[2], FF0_q[1], ~FF0_q[0], S);  // AND_Gate
  and and_5 (and_5_out, ~FF0_q[2], ~S);  // AND_Gate
  and and_6 (and_6_out, ~FF0_q[1], ~S);  // AND_Gate
  and and_7 (and_7_out, ~FF0_q[2], FF0_q[1], ~FF0_q[0]);  // AND_Gate
  and and_8 (and_8_out, FF0_q[2], ~FF0_q[1], FF0_q[0]);  // AND_Gate
  or or_1 (or_1_out, and_1_out, and_2_out);
  or or_2 (or_2_out, and_3_out, and_4_out);
  or or_3 (or_3_out, and_5_out, and_6_out, and_7_out);
  LED led_1 (.in(and_8_out));
  LED led_2 (.in(det_seq_111_1_det_out));
  det_seq_111 det_seq_111_1 (
    .rst(button_1_out), .seq_in(S), .clock(clock_1_out), .det_out(det_seq_111_1_det_out),
    .est_out(det_seq_111_1_est_out));
  Hex_Digit_Display hex_digit_display_2 (.value(det_seq_111_1_est_out));  // open: dp
endmodule

// VHDL entity det_seq_111, as the project stores it:
--------------------------------------------------------------------------------
-- UTFPR - Universidade Tecnológica Federal do Paraná - Curitiba - PR
-- Projeto : Detetor de sequência de bits
-- Arquivo : det_111.vhd
-- Autor   : prof. Gortan
-- Data    : Agosto 2021
--
--------------------------------------------------------------------------------
-- Descrição :
-- Circuito circuito detetor de sequência 01110
--
-- Esta versão utiliza o template sugerido pelo prof. Volney em
-- Circuit Design and Simulation with VHDL - 2nd ed. - Capítulo 11
-- O template separa claramente a parte combinacional da parte sequencial da
-- da máquina de estados.
--
-- abaixo, o processo denominado seq_proc realiza puramente a parte sequencial
--         o processo denominado comb_proc realiza puramente a parte combinacional
--
-- embora o processo comb_proc seja puramente combinacional, ele só executa quando
-- houver uma mudança de estado, a qual só ocorre síncrona com o clock devido ao
-- processo seq_proc
--------------------------------------------------------------------------------

library ieee;
  use ieee.std_logic_1164.all;
  use ieee.numeric_std.all;

entity det_seq_111 is
	port(
	------------------------------------------------------------------------------
	rst, seq_in, clock	: in  std_logic;                 	-- entradas clk e seq
	------------------------------------------------------------------------------
	det_out             : out std_logic;
	est_out 	        : out std_logic_vector(3 downto 0) -- display detectado
	);
end det_seq_111;

--------------------------------------------------------------------------------
architecture detetor of det_seq_111 is
	type estado is (A, B, C, D, E, F);
	signal estado_prs, prx_estado: estado;
	signal idx_estado: integer; -- índice do estado obtido com estado'POS(nome)
	-- especificamos a codificação do estado em binário (sequencial):
	attribute enum_encoding: string; -- o tipo de codificação do enum será 
	                                 -- especificado por meio de string
	attribute enum_encoding of estado: type is "sequential";
begin
	---------------------- Bloco de lógica sequencial: ------------------------
	seq_proc: process(clock,rst)
	begin
		if rst = '1' then estado_prs <= A;
		elsif clock = '1' and clock'event then
			estado_prs <= prx_estado;
		end if;
	end process seq_proc;

	---------------------- Bloco de lógica combinacional: ----------------------
	comb_proc: process(estado_prs,seq_in)
	begin
		-- Codificação do próximo estado em função do estado atual e da saída:
		case estado_prs is
			when A =>
				if seq_in = '0' then prx_estado <= B;
				else prx_estado <= A;
				end if;
			when B =>
				if seq_in = '1' then prx_estado <= C;
				else prx_estado <= B;
				end if;
			when C =>
				if seq_in = '1' then prx_estado <= D;
				else prx_estado <= B;
				end if;
			when D=>
				if seq_in = '1' then prx_estado <= E;
				else prx_estado <= B;
				end if;
			when E =>
				if seq_in = '1' then prx_estado <= A;
				else prx_estado <= F;
				end if;
			when F =>
				if seq_in = '1' then prx_estado <= C;
				else prx_estado <= B;
				end if;
		end case;
		----------------- Codificação da saída ------------------------
		case estado_prs IS
			WHEN F => det_out <= '1';
			WHEN OTHERS		=> det_out <= '0';
		end case;
	end process comb_proc;
	-- obtenção do número do estado para mostrar no display para debug:
	idx_estado<= estado'POS(estado_prs);
	-- atributo POS é do tipo integer - transformar para std_logic_vector:
	est_out <= std_logic_vector(to_unsigned(idx_estado, est_out'length));

end detetor;
