// Logisim project det_111.circ as structural Verilog
module sequencia (
  input  S
);

  wire and_1_out, and_2_out, and_3_out, and_4_out, and_5_out, and_6_out, and_7_out, and_8_out, and_9_out,
       and_10_out, button_1_out, clock_1_out, D0, D1, D2, det_seq_100010_1_det_out, not_1_out, not_2_out,
       not_3_out, not_4_out, Q0, Q1, Q2;
  wire [3:0] det_seq_100010_1_est_out;

  D_Flip_Flop FF0 (.D(D0), .clk(clock_1_out), .Q(Q0), .reset(button_1_out));  // open: Qn, preset
  Button button_1 (.out(button_1_out));
  Clock clock_1 (.out(clock_1_out));
  D_Flip_Flop FF1 (.D(D1), .clk(clock_1_out), .Q(Q1), .reset(button_1_out));  // open: Qn, preset
  not not_1 (not_1_out, Q2);
  not not_2 (not_2_out, Q1);
  not not_3 (not_3_out, Q0);
  not not_4 (not_4_out, S);
  D_Flip_Flop FF2 (.D(D2), .clk(clock_1_out), .Q(Q2), .reset(button_1_out));  // open: Qn, preset
  Hex_Digit_Display hex_digit_display_1 (.value({1'b0, Q2, Q1, Q0}));  // open: dp
  and and_1 (and_1_out, not_1_out, Q1, Q0, not_4_out);
  and and_2 (and_2_out, Q2, not_3_out, S);
  and and_3 (and_3_out, Q2, not_2_out, Q0, not_4_out);
  and and_4 (and_4_out, Q2, Q1, not_3_out);
  and and_5 (and_5_out, not_2_out, Q0, not_4_out);
  and and_6 (and_6_out, Q1, not_3_out, not_4_out);
  and and_7 (and_7_out, Q2, Q1, not_3_out);
  and and_8 (and_8_out, not_2_out, not_3_out, S);
  and and_9 (and_9_out, not_1_out, Q1, not_3_out, not_4_out);
  and and_10 (and_10_out, Q2, Q1, ~Q0);  // AND_Gate
  LED led_1 (.in(and_10_out));
  or or_1 (D2, and_1_out, and_2_out, and_3_out, and_4_out);
  or or_2 (D1, and_5_out, and_6_out, and_7_out);
  or or_3 (D0, and_8_out, and_9_out);
  det_seq_100010 det_seq_100010_1 (
    .rst(button_1_out), .seq_in(S), .clock(clock_1_out), .det_out(det_seq_100010_1_det_out),
    .est_out(det_seq_100010_1_est_out));
  LED led_2 (.in(det_seq_100010_1_det_out));
  Hex_Digit_Display hex_digit_display_2 (.value(det_seq_100010_1_est_out));  // open: dp
endmodule

// VHDL entity det_seq_100010, as the project stores it:
--------------------------------------------------------------------------------
-- UTFPR - Universidade Tecnológica Federal do Paraná - Curitiba - PR
-- Projeto : Detetor de sequência de bits
-- Arquivo : det_100010.vhd
-- Adaptação: Detector de sequência 100010 com Trava (Lock)
--------------------------------------------------------------------------------

library ieee;
  use ieee.std_logic_1164.all;
  use ieee.numeric_std.all;

entity det_seq_100010 is
    port(
    ------------------------------------------------------------------------------
    rst, seq_in, clock  : in  std_logic;                    -- entradas clk e seq
    ------------------------------------------------------------------------------
    det_out             : out std_logic;
    est_out             : out std_logic_vector(3 downto 0) -- display detectado
    );
end det_seq_100010;

--------------------------------------------------------------------------------
architecture detetor of det_seq_100010 is
    -- Adicionado estado G para comportar a sequência de 6 bits e a trava
    type estado is (A, B, C, D, E, F, G);
    signal estado_prs, prx_estado: estado;
    signal idx_estado: integer; 
    
    attribute enum_encoding: string; 
    attribute enum_encoding of estado: type is "sequential";
begin
    ---------------------- Bloco de lógica sequencial: ------------------------
    seq_proc: process(clock,rst)
    begin
        if rst = '1' then estado_prs <= A;
        elsif clock = '1' and clock'event then
            estado_prs <= prx_estado;
        end if;
    end process seq_proc;

    ---------------------- Bloco de lógica combinacional: ----------------------
    -- Sequência Alvo: 1 - 0 - 0 - 0 - 1 - 0
    comb_proc: process(estado_prs,seq_in)
    begin
        case estado_prs is
            -- Estado A: Inicial (0 bits)
            when A =>
                if seq_in = '1' then prx_estado <= B; -- Recebeu 1
                else prx_estado <= A;
                end if;

            -- Estado B: Já tem '1'
            when B =>
                if seq_in = '0' then prx_estado <= C; -- Recebeu 10
                else prx_estado <= B; -- Recebeu 11 (O último 1 serve de início)
                end if;

            -- Estado C: Já tem '10'
            when C =>
                if seq_in = '0' then prx_estado <= D; -- Recebeu 100
                else prx_estado <= B; -- Recebeu 101 (Erro, mas o 1 serve de início)
                end if;

            -- Estado D: Já tem '100'
            when D =>
                if seq_in = '0' then prx_estado <= E; -- Recebeu 1000
                else prx_estado <= B; -- Recebeu 1001 (Erro, mas o 1 serve de início)
                end if;

            -- Estado E: Já tem '1000'
            when E =>
                if seq_in = '1' then prx_estado <= F; -- Recebeu 10001
                else prx_estado <= A; -- Recebeu 10000 (Erro total, reseta)
                end if;

            -- Estado F: Já tem '10001'
            when F =>
                if seq_in = '0' then prx_estado <= G; -- Recebeu 100010 (COMPLETO)
                else prx_estado <= B; -- Recebeu 100011 (Erro, mas o 1 serve de início)
                end if;

            -- Estado G: Detecção Concluída (TRAVA)
            -- Conforme roteiro: "o sistema trava nesse estado"
            when G =>
                prx_estado <= G; -- Mantém no estado G independente da entrada

            when others =>
                prx_estado <= A;
        end case;

        ----------------- Codificação da saída ------------------------
        -- A saída det_out só vai para '1' quando a sequência completa é detectada (Estado G)
        case estado_prs IS
            WHEN G => det_out <= '1';
            WHEN OTHERS => det_out <= '0';
        end case;

    end process comb_proc;

    -- Debug: Número do estado para mostrar no display
    -- A=0, B=1, C=2, D=3, E=4, F=5, G=6
    idx_estado <= estado'POS(estado_prs);
    est_out <= std_logic_vector(to_unsigned(idx_estado, est_out'length));

end detetor;
