// Logisim project Aula_02_ex_01.circ as structural Verilog
module main (
  input  X,
  input  Y,
  output out_3,
  output out_4,
  output out_5,
  output out_6,
  output out_7,
  output out_8,
  output out_9,
  output out_10
);

  wire not_1_out, not_2_out, not_3_out, not_4_out;

  nor nor_1 (out_3, X, Y);
  nand nand_1 (out_5, X, Y);
  demorgan demorgan_1 (.X(X), .Y(Y), .A1(out_7), .A2(out_8), .B1(out_9), .B2(out_10));
  not not_1 (not_1_out, X);
  not not_2 (not_2_out, Y);
  not not_3 (not_3_out, X);
  not not_4 (not_4_out, Y);
  and and_1 (out_4, not_1_out, not_2_out);
  or or_1 (out_6, not_3_out, not_4_out);

  // Other names for the same wires on the sheet: xTunel = X; yTunel = Y
endmodule

// VHDL entity demorgan, as the project stores it:
--------------------------------------------------------------------------------
-- Project :
-- File    :
-- Autor   :
-- Date    :
--
--------------------------------------------------------------------------------
-- Description :
--
--------------------------------------------------------------------------------

LIBRARY ieee;
USE ieee.std_logic_1164.all;

ENTITY demorgan IS
  PORT (
  ------------------------------------------------------------------------------
  --Insert input ports below
    X      : IN  std_logic;                    -- input bit example
    Y      : IN  std_logic;                    -- input bit example
  ------------------------------------------------------------------------------
  --Insert output ports below
    A1        : OUT std_logic;                    -- output bit example
    A2        : OUT std_logic;                    -- output bit example
    B1        : OUT std_logic;                    -- output bit example
    B2        : OUT std_logic                    -- output bit example


    );
END demorgan;

--------------------------------------------------------------------------------
--Complete your VHDL description below
--------------------------------------------------------------------------------

ARCHITECTURE TypeArchitecture OF demorgan IS

BEGIN
	A1 <= NOT (X OR Y);
	A2 <= (NOT X) AND (NOT Y);
	B1 <= NOT (X AND Y);
	B2 <= (NOT X) OR (NOT Y);
	

END TypeArchitecture;
