// Logisim project Aula_02_ex_02.circ as structural Verilog
module main (
  input  in_1,
  input  in_2,
  input  in_3,
  input  in_4,
  output out_5,
  output out_6
);

  wire and_1_out, nor_1_out;

  nor nor_1 (nor_1_out, in_1, in_2);
  and and_1 (and_1_out, in_3, in_4);
  Aula_02_ex_02 aula_02_ex_02_1 (.a(in_1), .b(in_2), .c(in_3), .d(in_4), .z(out_6));
  and and_2 (out_5, nor_1_out, and_1_out);

  // Other names for the same wires on the sheet: A = in_1; B = in_2; C = in_3; D = in_4
endmodule

// VHDL entity Aula_02_ex_02, as the project stores it:
--------------------------------------------------------------------------------
-- Project :
-- File    :
-- Autor   :
-- Date    :
--
--------------------------------------------------------------------------------
-- Description :
--
--------------------------------------------------------------------------------

LIBRARY ieee;
USE ieee.std_logic_1164.all;

ENTITY Aula_02_ex_02 IS
  PORT (
  ------------------------------------------------------------------------------
  --Insert input ports below
    a      : IN  std_logic;                    -- input bit example
    b      : IN  std_logic;   
    c      : IN  std_logic;   
    d      : IN  std_logic;   
  ------------------------------------------------------------------------------
  --Insert output ports below
    z        : OUT std_logic                    -- output bit example
    
    );
END Aula_02_ex_02;

--------------------------------------------------------------------------------
--Complete your VHDL description below
--------------------------------------------------------------------------------

ARCHITECTURE TypeArchitecture OF Aula_02_ex_02 IS

BEGIN
	Z <= (NOT (A OR B)) AND ((C AND D));

END TypeArchitecture;
