// Logisim project Aula_02_ex_03.circ as structural Verilog
module main (
  input  A,
  input  B,
  input  C,
  input  D,
  output out_5,
  output out_6,
  output out_7,
  output out_8
);

  wire and_2_out, and_3_out, and_4_out, not_1_out, not_2_out, not_3_out, not_4_out, not_5_out, not_6_out,
       or_1_out;

  not not_1 (not_1_out, A);
  not not_2 (not_2_out, B);
  not not_3 (not_3_out, A);
  not not_4 (not_4_out, B);
  not not_5 (not_5_out, C);
  Aula_02_ex_03 aula_02_ex_03_1 (.A(A), .B(B), .C(C), .D(D), .X(out_7), .Y(out_8));
  or or_1 (or_1_out, not_1_out, not_2_out);
  not not_6 (not_6_out, or_1_out);
  and and_1 (out_5, not_6_out, B, C);
  and and_2 (and_2_out, not_3_out, not_4_out, not_5_out);
  and and_3 (and_3_out, A, not_4_out, not_5_out);
  and and_4 (and_4_out, not_3_out, not_4_out, D);
  or or_2 (out_6, and_2_out, and_3_out, and_4_out);

  // Other names for the same wires on the sheet: aTunel = A; bTunel = B; cTunel = C; dTunel = D
endmodule

// VHDL entity Aula_02_ex_03, as the project stores it:
--------------------------------------------------------------------------------
-- Project :
-- File    :
-- Autor   :
-- Date    :
--
--------------------------------------------------------------------------------
-- Description :
--
--------------------------------------------------------------------------------

LIBRARY ieee;
USE ieee.std_logic_1164.all;

ENTITY Aula_02_ex_03 IS
  PORT (
  ------------------------------------------------------------------------------
  --Insert input ports below
    A      : IN  std_logic;                    -- input bit example
    B      : IN  std_logic;                    -- input bit example
    C      : IN  std_logic;                    -- input bit example
    D      : IN  std_logic; 

  ------------------------------------------------------------------------------
  --Insert output ports below
    X        : OUT std_logic;                   -- output bit example
    Y        : OUT std_logic                   -- output bit example


    );
END Aula_02_ex_03;

--------------------------------------------------------------------------------
--Complete your VHDL description below
--------------------------------------------------------------------------------

ARCHITECTURE TypeArchitecture OF Aula_02_ex_03 IS

BEGIN

	X <= NOT(NOT A OR NOT B) AND B AND C;
	Y <= (NOT A AND NOT B AND NOT C) OR (A AND NOT B AND NOT C) OR (NOT A AND NOT B AND D);

END TypeArchitecture;
