// Logisim project Aula_03_ex_03.circ as structural Verilog
module main (
  input  [3:0] KLMN,
  input  [3:0] in_2
);

  wire clk_out;
  wire [3:0] cont_mod_16_q;
  wire [6:0] aula_03_ex_02_1_c_7s, aula_03_ex_02_2_c_7s, dec_7s_muxes_1_abcdefg;

  Clock clk (.out(clk_out));
  Counter #(.max('hf), .width(4)) cont_mod_16 (
    .clk(clk_out), .Q(cont_mod_16_q));  // open: clr, load, up, count, D, carry
  _7_Segment_Display u_7_segment_display_1 (
    .g(dec_7s_muxes_1_abcdefg[0]), .f(dec_7s_muxes_1_abcdefg[1]), .a(dec_7s_muxes_1_abcdefg[6]),
    .b(dec_7s_muxes_1_abcdefg[5]), .e(dec_7s_muxes_1_abcdefg[2]), .d(dec_7s_muxes_1_abcdefg[3]),
    .c(dec_7s_muxes_1_abcdefg[4]));  // open: dp
  dec_7s_muxes dec_7s_muxes_1 (.KLMN(KLMN), .ABCDEFG(dec_7s_muxes_1_abcdefg));
  _7_Segment_Display u_7_segment_display_2 (
    .g(aula_03_ex_02_1_c_7s[0]), .f(aula_03_ex_02_1_c_7s[1]), .a(aula_03_ex_02_1_c_7s[6]),
    .b(aula_03_ex_02_1_c_7s[5]), .e(aula_03_ex_02_1_c_7s[2]), .d(aula_03_ex_02_1_c_7s[3]),
    .c(aula_03_ex_02_1_c_7s[4]));  // open: dp
  Aula_03_ex_02 aula_03_ex_02_1 (.cnt_i(cont_mod_16_q), .c_7s(aula_03_ex_02_1_c_7s));
  _7_Segment_Display u_7_segment_display_3 (
    .g(aula_03_ex_02_2_c_7s[0]), .f(aula_03_ex_02_2_c_7s[1]), .a(aula_03_ex_02_2_c_7s[6]),
    .b(aula_03_ex_02_2_c_7s[5]), .e(aula_03_ex_02_2_c_7s[2]), .d(aula_03_ex_02_2_c_7s[3]),
    .c(aula_03_ex_02_2_c_7s[4]));  // open: dp
  Aula_03_ex_02 aula_03_ex_02_2 (.cnt_i(in_2), .c_7s(aula_03_ex_02_2_c_7s));
endmodule

module dec_7s_muxes (
  input  [3:0] KLMN,
  output [6:0] ABCDEFG
);

  Multiplexer #(.select(4)) multiplexer_1 (
    .in0(1'b1), .in1(1'b0), .in2(1'b1), .in3(1'b1), .in4(1'b0), .in5(1'b1), .in6(1'b1), .in7(1'b1),
    .in8(1'b1), .in9(1'b1), .in10(1'b1), .in11(1'b0), .in12(1'b1), .in13(1'b0), .in14(1'b1), .in15(1'b1),
    .out(ABCDEFG[6]), .sel(KLMN));
  Multiplexer #(.select(4)) multiplexer_2 (
    .in0(1'b1), .in1(1'b1), .in2(1'b1), .in3(1'b1), .in4(1'b1), .in5(1'b0), .in6(1'b0), .in7(1'b1),
    .in8(1'b1), .in9(1'b1), .in10(1'b1), .in11(1'b0), .in12(1'b0), .in13(1'b1), .in14(1'b0), .in15(1'b1),
    .out(ABCDEFG[5]), .sel(KLMN));
  Multiplexer #(.select(4)) multiplexer_3 (
    .in0(1'b1), .in1(1'b1), .in2(1'b0), .in3(1'b1), .in4(1'b1), .in5(1'b1), .in6(1'b1), .in7(1'b1),
    .in8(1'b1), .in9(1'b1), .in10(1'b1), .in11(1'b1), .in12(1'b0), .in13(1'b1), .in14(1'b1), .in15(1'b0),
    .out(ABCDEFG[4]), .sel(KLMN));
  Multiplexer #(.select(4)) multiplexer_4 (
    .in0(1'b1), .in1(1'b0), .in2(1'b1), .in3(1'b1), .in4(1'b0), .in5(1'b1), .in6(1'b1), .in7(1'b0),
    .in8(1'b1), .in9(1'b0), .in10(1'b0), .in11(1'b1), .in12(1'b1), .in13(1'b1), .in14(1'b1), .in15(1'b0),
    .out(ABCDEFG[3]), .sel(KLMN));
  Multiplexer #(.select(4)) multiplexer_5 (
    .in0(1'b1), .in1(1'b0), .in2(1'b1), .in3(1'b0), .in4(1'b0), .in5(1'b0), .in6(1'b1), .in7(1'b0),
    .in8(1'b1), .in9(1'b0), .in10(1'b1), .in11(1'b1), .in12(1'b1), .in13(1'b1), .in14(1'b1), .in15(1'b1),
    .out(ABCDEFG[2]), .sel(KLMN));
  Multiplexer #(.select(4)) multiplexer_6 (
    .in0(1'b1), .in1(1'b0), .in2(1'b0), .in3(1'b0), .in4(1'b1), .in5(1'b1), .in6(1'b1), .in7(1'b0),
    .in8(1'b1), .in9(1'b1), .in10(1'b1), .in11(1'b1), .in12(1'b1), .in13(1'b0), .in14(1'b1), .in15(1'b1),
    .out(ABCDEFG[1]), .sel(KLMN));
  Multiplexer #(.select(4)) multiplexer_7 (
    .in0(1'b0), .in1(1'b0), .in2(1'b1), .in3(1'b1), .in4(1'b1), .in5(1'b1), .in6(1'b1), .in7(1'b0),
    .in8(1'b1), .in9(1'b1), .in10(1'b1), .in11(1'b1), .in12(1'b0), .in13(1'b1), .in14(1'b1), .in15(1'b1),
    .out(ABCDEFG[0]), .sel(KLMN));

  // Other names for the same wires on the sheet: N = KLMN[0]; M = KLMN[1]; L = KLMN[2]; K = KLMN[3]; G = ABCDEFG[0];
  //   F = ABCDEFG[1]; E = ABCDEFG[2]; D = ABCDEFG[3]; C = ABCDEFG[4]; B = ABCDEFG[5]; A = ABCDEFG[6]
endmodule

// VHDL entity Aula_03_ex_02, as the project stores it:
LIBRARY ieee;
USE ieee.std_logic_1164.all;

ENTITY Aula_03_ex_02 IS
  PORT (
    cnt_i : IN  std_logic_vector(3 downto 0);       -- entrada
    c_7s  : OUT std_logic_vector(6 downto 0)       -- saída display
    
  );
END Aula_03_ex_02;

ARCHITECTURE TypeArchitecture OF Aula_03_ex_02 IS
BEGIN

  -- seleção correta: usa cnt_i, não o nome da entidade
  with cnt_i select
    c_7s <= "1111110" when "0000",  -- 0
            "0110000" when "0001",  -- 1
            "1101101" when "0010",  -- 2
            "1111001" when "0011",  -- 3
            "0110011" when "0100",  -- 4
            "1011011" when "0101",  -- 5
            "1011111" when "0110",  -- 6
            "1110000" when "0111",  -- 7
            "1111111" when "1000",  -- 8
            "1110011" when "1001",  -- 9
            "1110111" when "1010",  -- A
            "0011111" when "1011",  -- b
            "1001110" when "1100",  -- C
            "0111101" when "1101",  -- d
            "1011111" when "1110",  -- E
            "1100111" when "1111",  -- F
            "0000000" when others;  -- default (opcional)
            
END TypeArchitecture;
