// Logisim project Aula_03_ex_01.circ as structural Verilog
module main (
  input  [3:0] KLMN
);

  wire [6:0] dec_7s_muxes_1_abcdefg;

  _7_Segment_Display u_7_segment_display_1 (
    .g(dec_7s_muxes_1_abcdefg[0]), .f(dec_7s_muxes_1_abcdefg[1]), .a(dec_7s_muxes_1_abcdefg[6]),
    .b(dec_7s_muxes_1_abcdefg[5]), .e(dec_7s_muxes_1_abcdefg[2]), .d(dec_7s_muxes_1_abcdefg[3]),
    .c(dec_7s_muxes_1_abcdefg[4]));  // open: dp
  dec_7s_muxes dec_7s_muxes_1 (.KLMN(KLMN), .ABCDEFG(dec_7s_muxes_1_abcdefg));
endmodule

module dec_7s_muxes (
  input  [3:0] KLMN,
  output [6:0] ABCDEFG
);

  Multiplexer #(.select(4)) multiplexer_1 (
    .in0(1'b1), .in1(1'b0), .in2(1'b1), .in3(1'b1), .in4(1'b0), .in5(1'b1), .in6(1'b1), .in7(1'b1),
    .in8(1'b1), .in9(1'b1), .in10(1'b1), .in11(1'b0), .in12(1'b1), .in13(1'b0), .in14(1'b1), .in15(1'b1),
    .out(ABCDEFG[6]), .sel(KLMN));
  Multiplexer #(.select(4)) multiplexer_2 (
    .in0(1'b1), .in1(1'b1), .in2(1'b1), .in3(1'b1), .in4(1'b1), .in5(1'b0), .in6(1'b0), .in7(1'b1),
    .in8(1'b1), .in9(1'b1), .in10(1'b1), .in11(1'b0), .in12(1'b0), .in13(1'b1), .in14(1'b0), .in15(1'b1),
    .out(ABCDEFG[5]), .sel(KLMN));
  Multiplexer #(.select(4)) multiplexer_3 (
    .in0(1'b1), .in1(1'b1), .in2(1'b0), .in3(1'b1), .in4(1'b1), .in5(1'b1), .in6(1'b1), .in7(1'b1),
    .in8(1'b1), .in9(1'b1), .in10(1'b1), .in11(1'b1), .in12(1'b0), .in13(1'b1), .in14(1'b1), .in15(1'b0),
    .out(ABCDEFG[4]), .sel(KLMN));
  Multiplexer #(.select(4)) multiplexer_4 (
    .in0(1'b1), .in1(1'b0), .in2(1'b1), .in3(1'b1), .in4(1'b0), .in5(1'b1), .in6(1'b1), .in7(1'b0),
    .in8(1'b1), .in9(1'b0), .in10(1'b0), .in11(1'b1), .in12(1'b1), .in13(1'b1), .in14(1'b1), .in15(1'b0),
    .out(ABCDEFG[3]), .sel(KLMN));
  Multiplexer #(.select(4)) multiplexer_5 (
    .in0(1'b1), .in1(1'b0), .in2(1'b1), .in3(1'b0), .in4(1'b0), .in5(1'b0), .in6(1'b1), .in7(1'b0),
    .in8(1'b1), .in9(1'b0), .in10(1'b1), .in11(1'b1), .in12(1'b1), .in13(1'b1), .in14(1'b1), .in15(1'b1),
    .out(ABCDEFG[2]), .sel(KLMN));
  Multiplexer #(.select(4)) multiplexer_6 (
    .in0(1'b1), .in1(1'b0), .in2(1'b0), .in3(1'b0), .in4(1'b1), .in5(1'b1), .in6(1'b1), .in7(1'b0),
    .in8(1'b1), .in9(1'b1), .in10(1'b1), .in11(1'b1), .in12(1'b1), .in13(1'b0), .in14(1'b1), .in15(1'b1),
    .out(ABCDEFG[1]), .sel(KLMN));
  Multiplexer #(.select(4)) multiplexer_7 (
    .in0(1'b0), .in1(1'b0), .in2(1'b1), .in3(1'b1), .in4(1'b1), .in5(1'b1), .in6(1'b1), .in7(1'b0),
    .in8(1'b1), .in9(1'b1), .in10(1'b1), .in11(1'b1), .in12(1'b0), .in13(1'b1), .in14(1'b1), .in15(1'b1),
    .out(ABCDEFG[0]), .sel(KLMN));

  // Other names for the same wires on the sheet: N = KLMN[0]; M = KLMN[1]; L = KLMN[2]; K = KLMN[3]; G = ABCDEFG[0];
  //   F = ABCDEFG[1]; E = ABCDEFG[2]; D = ABCDEFG[3]; C = ABCDEFG[4]; B = ABCDEFG[5]; A = ABCDEFG[6]
endmodule

// VHDL entity Aula_03_ex_01, as the project stores it:
--------------------------------------------------------------------------------
-- Project :
-- File    :
-- Autor   :
-- Date    :
--
--------------------------------------------------------------------------------
-- Description :
--
--------------------------------------------------------------------------------

LIBRARY ieee;
USE ieee.std_logic_1164.all;

ENTITY Aula_03_ex_01 IS
  PORT (
  ------------------------------------------------------------------------------
  --Insert input ports below
    clock      : IN  std_logic;                    -- input bit example
    val        : IN  std_logic_vector(3 DOWNTO 0); -- input vector example
  ------------------------------------------------------------------------------
  --Insert output ports below
    max        : OUT std_logic;                    -- output bit example
    cpt        : OUT std_logic_vector(3 DOWNTO 0)  -- output vector example
    );
END Aula_03_ex_01;

--------------------------------------------------------------------------------
--Complete your VHDL description below
--------------------------------------------------------------------------------

ARCHITECTURE TypeArchitecture OF Aula_03_ex_01 IS

BEGIN


END TypeArchitecture;
