// Logisim project aula1 (1).circ as structural Verilog
module main (
  input  in_1,
  input  in_2,
  input  in_3,
  input  in_4,
  input  in_5,
  input  in_6,
  input  in_7,
  input  in_8,
  input  in_9,
  input  in_10,
  input  in_11,
  input  in_12,
  input  x,
  input  y,
  input  in_15,
  output NAND,
  output AND,
  output NOR,
  output OR,
  output XNOR,
  output NOT,
  output out_22,
  output out_23,
  output out_24,
  output out_25,
  output z,
  output out_27,
  output out_28,
  output out_29
);

  wire And1_out, And2_out, and_2_out, not_2_out, not_3_out, or_2_out, xor_1_out;

  and and_1 (AND, in_2, in_4);
  or or_1 (OR, in_6, in_8);
  not not_1 (NOT, in_10);
  and And1 (And1_out, in_12, not_2_out);
  not not_2 (not_2_out, in_15);
  not not_3 (not_3_out, in_12);
  and And2 (And2_out, not_3_out, in_15);
  or or1 (z, And1_out, And2_out);
  and and_2 (and_2_out, in_1, in_3);
  or or_2 (or_2_out, in_5, in_7);
  xor xor_1 (xor_1_out, in_9, in_11);
  not not_4 (NAND, and_2_out);
  not not_5 (NOR, or_2_out);
  not not_6 (XNOR, xor_1_out);
  VHDL_XOR vhdl_xor_1 (
    .X(x), .Y(y), .zXOR(out_22), .zAND(out_23), .zOR(out_24), .zNOT(out_25), .zNAND(out_27), .zNOR(out_28),
    .zXNOR(out_29));

  // Notes on the sheet:
  //   Xor
endmodule

// VHDL entity VHDL_XOR, as the project stores it:
--------------------------------------------------------------------------------
-- Project :
-- File    :
-- Autor   :
-- Date    :
--
--------------------------------------------------------------------------------
-- Description :
--
--------------------------------------------------------------------------------

LIBRARY ieee;
USE ieee.std_logic_1164.all;

ENTITY VHDL_XOR IS
  PORT (
  ------------------------------------------------------------------------------
    X	: IN std_logic;
    Y	: IN std_logic;
  ------------------------------------------------------------------------------
    zXOR	: OUT std_logic;
    zAND	: OUT std_logic;
    zOR	: OUT std_logic;
    zNOT	: OUT std_logic;
    zNAND	: OUT std_logic;
    zNOR	: OUT std_logic;
    zXNOR	: OUT std_logic
    );
END VHDL_XOR;

--------------------------------------------------------------------------------
--Complete your VHDL description below
--------------------------------------------------------------------------------

ARCHITECTURE TypeArchitecture OF VHDL_XOR IS

BEGIN

	zXOR <= X XOR Y;
	zAND <= X AND Y;
	zOR <= X OR Y;
	zNOT <= NOT Y;
	zNAND <= X NAND Y;
	zNOR <= X NOR Y;
	zXNOR <= X XNOR Y;


END TypeArchitecture;
