// Logisim project aula2.circ as structural Verilog
module main (
  input  [3:0] Bin_In,
  output [3:0] Gray_out,
  output [3:0] Gray_out_VHDL
);

  // Probe on Bin_In
  // Probe on Gray_out_VHDL
  xor xor_1 (Gray_out[2], Bin_In[3], Bin_In[2]);
  xor xor_2 (Gray_out[1], Bin_In[2], Bin_In[1]);
  Conv_bin_gray conv_bin_gray_1 (.BIN_IN(Bin_In), .GRAY_OUT_VHDL(Gray_out_VHDL));
  xor xor_3 (Gray_out[0], Bin_In[1], Bin_In[0]);

  assign Gray_out[3] = Bin_In[3];

  // Other names for the same wires on the sheet: G_o[3:0] = Gray_out_VHDL
endmodule

// VHDL entity Conv_bin_gray, as the project stores it:
--------------------------------------------------------------------------------
-- Project :
-- File    :
-- Autor   :
-- Date    :
--
--------------------------------------------------------------------------------
-- Description :
--
--------------------------------------------------------------------------------

LIBRARY ieee;
USE ieee.std_logic_1164.all;

ENTITY Conv_bin_gray IS
  PORT (
  ------------------------------------------------------------------------------
	BIN_IN	: IN std_logic_vector(3 downto 0);
  ------------------------------------------------------------------------------
	GRAY_OUT_VHDL	: OUT std_logic_vector(3 downto 0)
    );
END Conv_bin_gray;

--------------------------------------------------------------------------------
--Complete your VHDL description below
--------------------------------------------------------------------------------

ARCHITECTURE TypeArchitecture OF Conv_bin_gray IS

BEGIN

 ------------------------------------------------------------------------------
	GRAY_OUT_VHDL(3) <=  BIN_IN(3);
	GRAY_OUT_VHDL(2) <= BIN_IN(3) XOR BIN_IN(2);
	GRAY_OUT_VHDL(1) <= BIN_IN(1) XOR BIN_IN(2);
	GRAY_OUT_VHDL(0) <= BIN_IN(0) XOR BIN_IN(1);
 ------------------------------------------------------------------------------	

END TypeArchitecture;
