// Logisim project Aula_02_ex_02.circ as structural Verilog
module main (
  input  A,
  input  B,
  input  C,
  input  D,
  output Z
);

  wire and_1_out, nor_1_out;

  nor nor_1 (nor_1_out, A, B);
  and and_1 (and_1_out, C, D);
  and and_2 (Z, nor_1_out, and_1_out);
endmodule

// VHDL entity Aula_02_ex_02, as the project stores it:
--------------------------------------------------------------------------------
-- Project :
-- File    :
-- Autor   :
-- Date    :
--
--------------------------------------------------------------------------------
-- Description :
--
--------------------------------------------------------------------------------

LIBRARY ieee;
USE ieee.std_logic_1164.all;

ENTITY Aula_02_ex_02 IS
  PORT (
  ------------------------------------------------------------------------------
  --Insert input ports below
    A      : IN  std_logic;
    B      : IN  std_logic;
    C      : IN  std_logic;
    D      : IN  std_logic;

    Z	: OUT std_logic
    
    );
END Aula_02_ex_02;

--------------------------------------------------------------------------------
--Complete your VHDL description below
--------------------------------------------------------------------------------

ARCHITECTURE TypeArchitecture OF Aula_02_ex_02 IS

BEGIN

	Z <= (NOT (A OR B)) AND (C AND D);

END TypeArchitecture;
